// Logisim project CPU.circ as structural Verilog: 18 circuits, main circuit main
module main (
  input  in_1,
  input  in_2,
  input  in_3,
  input  in_4,
  input  in_5,
  input  in_6,
  input  in_7,
  input  in_8,
  input  in_9,
  input  in_10,
  output Instructing,
  output Fetching,
  output out_13
);

  wire and_1_out, and_2_out, and_3_out, and_4_out, and_5_out, and_6_out, and_7_out, and_8_out, buffer_6_out,
       button_1_out, clock_1_out, CPU_ON, cu_1_alu_exe, cu_1_alu_flag, cu_1_alu_l, cu_1_alu_o, cu_1_alu_r,
       cu_1_ar_in, cu_1_branch_sign, cu_1_dr_out, cu_1_inpt, cu_1_ir, cu_1_mar_in, cu_1_mar_out, cu_1_mbr_in,
       cu_1_mbr_out, cu_1_pc_a_i, cu_1_pc_inc, cu_1_pc_out, cu_1_pnt, cu_1_r_w, cu_1_ram_r, cu_1_ram_w,
       cu_1_reg0, cu_1_reg1, cu_1_stat, LOAD_PRGRM_out, not_1_out, not_2_out, not_3_out, or_1_out, or_2_out,
       or_3_out, or_4_out, or_5_out, or_6_out, or_7_out, prog_rom_ver2_1_a_w, prog_rom_ver2_1_ram_m,
       prog_rom_ver2_1_ram_m_w, selector_out_4;
  wire [1:0] cu_1_dr_in;
  wire [6:0] display_1_out_2, display_1_out_3, display_1_out_4;
  wire [7:0] ADDR_o, alu_1_flags, alu_1_o, buffer_1_out, buffer_4_out, controlled_buffer_1_out,
       controlled_buffer_3_out, controlled_buffer_6_out, controlled_buffer_7_out, controlled_buffer_9_out,
       controlled_buffer_12_out, controlled_buffer_13_out, cu_1_pc_a_o, cu_1_ram_a, DATA_o, general_reg_1_o,
       general_reg_2_o, incby1_1_to_pc, input_buffer_1_out_11, MAR_o, MBR_o, mode_reg_1_o, multiplexer_1_out,
       multiplexer_2_out, multiplexer_3_out, pc_1_o, prog_rom_ver2_1_addr_o, prog_rom_ver2_1_instr_o, R0_o,
       R1_o, ram_16bytes_1_a0000, ram_16bytes_1_a0001, ram_16bytes_1_a0010, ram_16bytes_1_a0011,
       ram_16bytes_1_a0100, ram_16bytes_1_a0101, ram_16bytes_1_a0110, ram_16bytes_1_a0111,
       ram_16bytes_1_a1000, ram_16bytes_1_a1001, ram_16bytes_1_a1010, ram_16bytes_1_a1011,
       ram_16bytes_1_a1100, ram_16bytes_1_a1101, ram_16bytes_1_a1110, ram_16bytes_1_a1111,
       ram_16bytes_1_data_output;

  Button LOAD_PRGRM (.out(LOAD_PRGRM_out));
  Button button_1 (.out(button_1_out));
  PROG_ROM_VER2 prog_rom_ver2_1 (
    .RESET(button_1_out), .Tick_on(LOAD_PRGRM_out), .Working(out_13), .RAM_M(prog_rom_ver2_1_ram_m),
    .RAM_M_W(prog_rom_ver2_1_ram_m_w), .Instr_O(prog_rom_ver2_1_instr_o), .Addr_O(prog_rom_ver2_1_addr_o),
    .A_W(prog_rom_ver2_1_a_w), .D_W(cu_1_dr_in[1]), .CPU_ON(CPU_ON));
  Clock clock_1 (.out(clock_1_out));
  // Probe on ram_16bytes_1_data_output
  // Probe on DATA_o
  // Probe on ADDR_o
  // Probe on mode_reg_1_o
  GENERAL_REG DATA (.O(DATA_o), .I(multiplexer_1_out), .in_1(or_4_out), .in_3(button_1_out));
  Multiplexer #(.select(2), .width(8), .enable("false")) multiplexer_1 (
    .in0(ram_16bytes_1_data_output), .in1(controlled_buffer_1_out), .in2(prog_rom_ver2_1_instr_o),
    .out(multiplexer_1_out), .sel(cu_1_dr_in));  // open: in3
  Multiplexer #(.width(8), .enable("false")) multiplexer_2 (
    .in0(controlled_buffer_3_out), .in1(prog_rom_ver2_1_addr_o), .out(multiplexer_2_out),
    .sel(prog_rom_ver2_1_a_w));
  GENERAL_REG ADDR (.O(ADDR_o), .I(multiplexer_2_out), .in_1(or_5_out), .in_3(button_1_out));
  MODE_REG mode_reg_1 (.O(mode_reg_1_o), .in_2(or_2_out), .I(or_1_out));
  or or_1 (or_1_out, prog_rom_ver2_1_ram_m, cu_1_ram_w);
  or or_2 (or_2_out, prog_rom_ver2_1_ram_m_w, or_3_out);
  or or_3 (or_3_out, cu_1_ram_w, cu_1_ram_r);
  INPUT_BUFFER input_buffer_1 (
    .in_5(in_5), .in_7(in_7), .in_1(in_1), .in_9(in_9), .in_8(in_8), .in_2(in_2), .in_3(in_3), .in_6(in_6),
    .in_10(in_10), .out_11(input_buffer_1_out_11), .in_4(in_4));
  assign controlled_buffer_1_out = cu_1_inpt ? input_buffer_1_out_11 : 8'bz;  // Controlled_Buffer controlled_buffer_1
  RAM_16bytes ram_16bytes_1 (
    .in_4(mode_reg_1_o), .in_5(DATA_o), .in_3(ADDR_o), .data_output(ram_16bytes_1_data_output),
    .clk(clock_1_out), .A0000(ram_16bytes_1_a0000), .A0001(ram_16bytes_1_a0001), .A0010(ram_16bytes_1_a0010),
    .A0011(ram_16bytes_1_a0011), .A0100(ram_16bytes_1_a0100), .A0101(ram_16bytes_1_a0101),
    .A0110(ram_16bytes_1_a0110), .A0111(ram_16bytes_1_a0111), .A1000(ram_16bytes_1_a1000),
    .A1001(ram_16bytes_1_a1001), .A1010(ram_16bytes_1_a1010), .A1011(ram_16bytes_1_a1011),
    .A1100(ram_16bytes_1_a1100), .A1101(ram_16bytes_1_a1101), .A1110(ram_16bytes_1_a1110),
    .A1111(ram_16bytes_1_a1111), .in_1(button_1_out));
  or or_4 (or_4_out, or_6_out, cu_1_dr_in[1]);
  or or_5 (or_5_out, cu_1_ar_in, prog_rom_ver2_1_a_w);
  // Probe on ram_16bytes_1_a0000
  // Probe on ram_16bytes_1_a0010
  // Probe on ram_16bytes_1_a0100
  // Probe on ram_16bytes_1_a0110
  // Probe on ram_16bytes_1_a1000
  // Probe on ram_16bytes_1_a1010
  // Probe on ram_16bytes_1_a1100
  // Probe on ram_16bytes_1_a1110
  or or_6 (or_6_out, cu_1_dr_in[0], cu_1_ram_r);
  // Probe on general_reg_1_o
  GENERAL_REG general_reg_1 (.O(general_reg_1_o), .I(controlled_buffer_1_out), .in_1(cu_1_pnt), .in_3(button_1_out));
  // Probe on ram_16bytes_1_a0001
  // Probe on ram_16bytes_1_a0011
  // Probe on ram_16bytes_1_a0101
  // Probe on ram_16bytes_1_a0111
  // Probe on ram_16bytes_1_a1001
  // Probe on ram_16bytes_1_a1011
  // Probe on ram_16bytes_1_a1101
  // Probe on ram_16bytes_1_a1111
  assign controlled_buffer_1_out = cu_1_dr_out ? DATA_o : 8'bz;  // Controlled_Buffer controlled_buffer_2
  assign controlled_buffer_3_out = cu_1_ar_in ? controlled_buffer_1_out : 8'bz;  // Controlled_Buffer controlled_buffer_3
  DISPLAY display_1 (.out_2(display_1_out_2), .out_4(display_1_out_4), .in_1(general_reg_1_o), .out_3(display_1_out_3));
  _7_Segment_Display u_7_segment_display_1 (
    .g(display_1_out_3[6]), .f(display_1_out_3[5]), .a(display_1_out_3[0]), .b(display_1_out_3[1]),
    .e(display_1_out_3[4]), .d(display_1_out_3[3]), .c(display_1_out_3[2]));  // open: dp
  _7_Segment_Display u_7_segment_display_2 (
    .g(display_1_out_2[6]), .f(display_1_out_2[5]), .a(display_1_out_2[0]), .b(display_1_out_2[1]),
    .e(display_1_out_2[4]), .d(display_1_out_2[3]), .c(display_1_out_2[2]));  // open: dp
  assign buffer_1_out = controlled_buffer_1_out;  // Buffer buffer_1, 8 bits wide
  assign buffer_1_out = controlled_buffer_1_out;  // Buffer buffer_2, 8 bits wide
  _7_Segment_Display u_7_segment_display_3 (
    .g(display_1_out_4[6]), .f(display_1_out_4[5]), .a(display_1_out_4[0]), .b(display_1_out_4[1]),
    .e(display_1_out_4[4]), .d(display_1_out_4[3]), .c(display_1_out_4[2]));  // open: dp
  assign buffer_1_out = buffer_4_out;  // Buffer buffer_3, 8 bits wide
  // Probe on MAR_o
  GENERAL_REG MAR (.O(MAR_o), .I(buffer_1_out), .in_1(cu_1_mar_in), .in_3(button_1_out));
  // Probe on MBR_o
  GENERAL_REG MBR (.O(MBR_o), .I(buffer_1_out), .in_1(cu_1_mbr_in), .in_3(button_1_out));
  assign controlled_buffer_1_out = cu_1_mar_out ? MAR_o : 8'bz;  // Controlled_Buffer controlled_buffer_4
  assign controlled_buffer_1_out = cu_1_mbr_out ? MBR_o : 8'bz;  // Controlled_Buffer controlled_buffer_5
  // Probe on cu_1_pc_a_o
  assign buffer_4_out = controlled_buffer_1_out;  // Buffer buffer_4, 8 bits wide
  assign buffer_4_out = controlled_buffer_1_out;  // Buffer buffer_5, 8 bits wide
  and and_1 (and_1_out, cu_1_reg0, cu_1_r_w);
  assign controlled_buffer_6_out = and_1_out ? buffer_4_out : 8'bz;  // Controlled_Buffer controlled_buffer_6
  // Probe on R1_o
  // Probe on R0_o
  // Probe on incby1_1_to_pc
  INCBY1 incby1_1 (.to_PC(incby1_1_to_pc), .from_PC(pc_1_o), .Inc(and_7_out));
  Multiplexer #(.width(8), .enable("false")) multiplexer_3 (
    .in0(incby1_1_to_pc), .in1(cu_1_pc_a_o), .out(multiplexer_3_out), .sel(selector_out_4));
  selector_thing selector (.in_3(cu_1_branch_sign), .in_1(cu_1_pc_a_i), .in_2(buffer_4_out), .out_4(selector_out_4));
  assign controlled_buffer_7_out = buffer_6_out ? buffer_4_out : 8'bz;  // Controlled_Buffer controlled_buffer_7
  assign buffer_4_out = and_2_out ? R0_o : 8'bz;  // Controlled_Buffer controlled_buffer_8
  GENERAL_REG R0 (.O(R0_o), .I(controlled_buffer_6_out), .in_1(and_3_out), .in_3(button_1_out));
  and and_2 (and_2_out, not_1_out, cu_1_reg0);
  and and_3 (and_3_out, cu_1_reg0, cu_1_r_w);
  PC pc_1 (.W(or_7_out), .I(multiplexer_3_out), .O(pc_1_o), .in_3(button_1_out));
  T_Flip_Flop t_ff_1 (.T(1'b1), .clk(cu_1_reg1));  // open: Q, Qn, reset, preset
  and and_4 (and_4_out, cu_1_reg1, cu_1_r_w);
  assign controlled_buffer_9_out = and_4_out ? buffer_4_out : 8'bz;  // Controlled_Buffer controlled_buffer_9
  not not_1 (not_1_out, cu_1_r_w);
  assign buffer_4_out = cu_1_pc_out ? pc_1_o : 8'bz;  // Controlled_Buffer controlled_buffer_10
  or or_7 (or_7_out, cu_1_pc_inc, selector_out_4);
  // Probe on general_reg_2_o
  GENERAL_REG general_reg_2 (
    .O(general_reg_2_o), .I(controlled_buffer_7_out), .in_1(buffer_6_out), .in_3(button_1_out));
  buf buffer_6 (buffer_6_out, cu_1_ir);
  assign buffer_4_out = and_5_out ? R1_o : 8'bz;  // Controlled_Buffer controlled_buffer_11
  GENERAL_REG R1 (.O(R1_o), .I(controlled_buffer_9_out), .in_1(and_6_out), .in_3(button_1_out));
  and and_5 (and_5_out, not_2_out, cu_1_reg1);
  and and_6 (and_6_out, cu_1_reg1, cu_1_r_w);
  // Probe on pc_1_o
  not not_2 (not_2_out, cu_1_r_w);
  ALU alu_1 (
    .O(alu_1_o), .L(buffer_4_out), .R(buffer_4_out), .Mode(cu_1_alu_flag), .Flags(alu_1_flags),
    .R_W(cu_1_alu_r), .L_W(cu_1_alu_l), .ALU_ACTV(cu_1_alu_exe), .in_7(button_1_out));
  assign buffer_4_out = controlled_buffer_13_out;  // Buffer buffer_7, 8 bits wide
  assign buffer_4_out = controlled_buffer_12_out;  // Buffer buffer_8, 8 bits wide
  assign controlled_buffer_12_out = cu_1_stat ? alu_1_flags : 8'bz;  // Controlled_Buffer controlled_buffer_12
  // Probe on alu_1_flags
  assign controlled_buffer_13_out = cu_1_alu_o ? alu_1_o : 8'bz;  // Controlled_Buffer controlled_buffer_13
  // Probe on alu_1_o
  CU cu_1 (
    .MAR_IN(cu_1_mar_in), .BRANCH_SIGN(cu_1_branch_sign), .DR_IN(cu_1_dr_in[0]), .AR_IN(cu_1_ar_in),
    .RAM_A(cu_1_ram_a), .PC_A_I(cu_1_pc_a_i), .MBR_OUT(cu_1_mbr_out), .ALU_R(cu_1_alu_r), .ALU_L(cu_1_alu_l),
    .Reg1(cu_1_reg1), .PC_OUT(cu_1_pc_out), .PC_INC(cu_1_pc_inc), .ALU_O(cu_1_alu_o), .STAT(cu_1_stat),
    .RAM_W(cu_1_ram_w), .MBR_IN(cu_1_mbr_in), .ALU_EXE(cu_1_alu_exe), .Reg0(cu_1_reg0), .RAM_R(cu_1_ram_r),
    .ALU_FLAG(cu_1_alu_flag), .MAR_OUT(cu_1_mar_out), .IRin(general_reg_2_o), .DR_OUT(cu_1_dr_out),
    .R_W(cu_1_r_w), .PC_A_O(cu_1_pc_a_o), .Initial_On_Keep_On(CPU_ON), .IR(cu_1_ir), .PNT(cu_1_pnt),
    .INPT(cu_1_inpt), .Instructing(Instructing), .Fetching(Fetching), .RESET_AFTER_RUN(button_1_out));
  T_Flip_Flop t_ff_2 (.T(1'b1), .clk(cu_1_ir));  // open: Q, Qn, reset, preset
  and and_7 (and_7_out, cu_1_mbr_out, cu_1_ir);
  not not_3 (not_3_out, cu_1_pc_out);
  and and_8 (and_8_out, cu_1_mar_in, not_3_out);
  assign buffer_4_out = and_8_out ? cu_1_ram_a : 8'bz;  // Controlled_Buffer controlled_buffer_14

  // Notes on the sheet:
  //   RESET
  //   LOAD PROGRAM & EXE
  //   sys_bus
  //   CPU BUS
endmodule

module mem_cell (
  input  \input ,
  input  mode,
  input  select,
  input  in_4,
  input  in_5,
  output Pin_Read,
  output \output 
);

  wire and_1_out, and_2_out, not_1_out, not_2_out;

  and and_1 (and_1_out, mode, select, not_1_out);
  not not_1 (not_1_out, \input );
  S_R_Flip_Flop s_r_ff_1 (.S(and_2_out), .R(and_1_out), .clk(in_4), .Q(Pin_Read), .reset(in_5));  // open: Qn, preset
  and and_2 (and_2_out, \input , mode, select);
  not not_2 (not_2_out, mode);
  and and_3 (\output , Pin_Read, not_2_out, select);

  // Notes on the sheet:
  //   clk
endmodule

module RAM_16bytes (
  input  in_1,
  input  clk,
  input  [7:0] in_3,
  input  [7:0] in_4,
  input  [7:0] in_5,
  output [7:0] A0000,
  output [7:0] A0001,
  output [7:0] A0010,
  output [7:0] A0100,
  output [7:0] A0101,
  output [7:0] A0110,
  output [7:0] A0111,
  output [7:0] A1000,
  output [7:0] A1001,
  output [7:0] A1010,
  output [7:0] A1011,
  output [7:0] A1100,
  output [7:0] A1101,
  output [7:0] A1110,
  output [7:0] A1111,
  output [7:0] A0011,
  output [7:0] data_output
);

  wire I0000_out, I0001_out, I0010_out, I0011_out, I0100_out, I0101_out, I0110_out, I0111_out, I111_out,
       I1000_out, I1001_out, I1010_out, I1011_out, I1100_out, I1101_out, I1110_out, mem_cell_1_output,
       mem_cell_2_output, mem_cell_3_output, mem_cell_4_output, mem_cell_5_output, mem_cell_6_output,
       mem_cell_7_output, mem_cell_8_output, mem_cell_9_output, mem_cell_10_output, mem_cell_11_output,
       mem_cell_12_output, mem_cell_13_output, mem_cell_14_output, mem_cell_15_output, mem_cell_16_output,
       mem_cell_17_output, mem_cell_18_output, mem_cell_19_output, mem_cell_20_output, mem_cell_21_output,
       mem_cell_22_output, mem_cell_23_output, mem_cell_24_output, mem_cell_25_output, mem_cell_26_output,
       mem_cell_27_output, mem_cell_28_output, mem_cell_29_output, mem_cell_30_output, mem_cell_31_output,
       mem_cell_32_output, mem_cell_33_output, mem_cell_34_output, mem_cell_35_output, mem_cell_36_output,
       mem_cell_37_output, mem_cell_38_output, mem_cell_39_output, mem_cell_40_output, mem_cell_41_output,
       mem_cell_42_output, mem_cell_43_output, mem_cell_44_output, mem_cell_45_output, mem_cell_46_output,
       mem_cell_47_output, mem_cell_48_output, mem_cell_49_output, mem_cell_50_output, mem_cell_51_output,
       mem_cell_52_output, mem_cell_53_output, mem_cell_54_output, mem_cell_55_output, mem_cell_56_output,
       mem_cell_57_output, mem_cell_58_output, mem_cell_59_output, mem_cell_60_output, mem_cell_61_output,
       mem_cell_62_output, mem_cell_63_output, mem_cell_64_output, mem_cell_65_output, mem_cell_66_output,
       mem_cell_67_output, mem_cell_68_output, mem_cell_69_output, mem_cell_70_output, mem_cell_71_output,
       mem_cell_72_output, mem_cell_73_output, mem_cell_74_output, mem_cell_75_output, mem_cell_76_output,
       mem_cell_77_output, mem_cell_78_output, mem_cell_79_output, mem_cell_80_output, mem_cell_81_output,
       mem_cell_82_output, mem_cell_83_output, mem_cell_84_output, mem_cell_85_output, mem_cell_86_output,
       mem_cell_87_output, mem_cell_88_output, mem_cell_89_output, mem_cell_90_output, mem_cell_91_output,
       mem_cell_92_output, mem_cell_93_output, mem_cell_94_output, mem_cell_95_output, mem_cell_96_output,
       mem_cell_97_output, mem_cell_98_output, mem_cell_99_output, mem_cell_100_output, mem_cell_101_output,
       mem_cell_102_output, mem_cell_103_output, mem_cell_104_output, mem_cell_105_output,
       mem_cell_106_output, mem_cell_107_output, mem_cell_108_output, mem_cell_109_output,
       mem_cell_110_output, mem_cell_111_output, mem_cell_112_output, mem_cell_113_output,
       mem_cell_114_output, mem_cell_115_output, mem_cell_116_output, mem_cell_117_output,
       mem_cell_118_output, mem_cell_119_output, mem_cell_120_output, mem_cell_121_output,
       mem_cell_122_output, mem_cell_123_output, mem_cell_124_output, mem_cell_125_output,
       mem_cell_126_output, mem_cell_127_output, mem_cell_128_output, not_1_out, not_2_out, not_3_out,
       not_4_out, or_1_out, or_2_out, or_3_out, or_4_out, or_5_out, or_6_out, or_7_out, or_8_out, or_9_out,
       or_10_out, or_11_out, or_12_out, or_13_out, or_14_out, or_15_out, or_16_out, or_17_out, or_18_out,
       or_19_out, or_20_out, or_21_out, or_22_out, or_23_out, or_24_out;

  not not_1 (not_1_out, in_3[1]);
  not not_2 (not_2_out, in_3[3]);
  not not_3 (not_3_out, in_3[0]);
  not not_4 (not_4_out, in_3[2]);
  and I0000 (I0000_out, not_2_out, not_4_out, not_1_out, not_3_out);
  mem_cell mem_cell_1 (
    .\input (in_5[0]), .mode(in_4[0]), .select(I0000_out), .\output (mem_cell_1_output), .in_4(clk),
    .Pin_Read(A0000[0]), .in_5(in_1));
  mem_cell mem_cell_2 (
    .\input (in_5[1]), .mode(in_4[0]), .select(I0000_out), .\output (mem_cell_2_output), .in_4(clk),
    .Pin_Read(A0000[1]), .in_5(in_1));
  mem_cell mem_cell_3 (
    .\input (in_5[2]), .mode(in_4[0]), .select(I0000_out), .\output (mem_cell_3_output), .in_4(clk),
    .Pin_Read(A0000[2]), .in_5(in_1));
  mem_cell mem_cell_4 (
    .\input (in_5[3]), .mode(in_4[0]), .select(I0000_out), .\output (mem_cell_4_output), .in_4(clk),
    .Pin_Read(A0000[3]), .in_5(in_1));
  mem_cell mem_cell_5 (
    .\input (in_5[4]), .mode(in_4[0]), .select(I0000_out), .\output (mem_cell_5_output), .in_4(clk),
    .Pin_Read(A0000[4]), .in_5(in_1));
  mem_cell mem_cell_6 (
    .\input (in_5[5]), .mode(in_4[0]), .select(I0000_out), .\output (mem_cell_6_output), .in_4(clk),
    .Pin_Read(A0000[5]), .in_5(in_1));
  mem_cell mem_cell_7 (
    .\input (in_5[6]), .mode(in_4[0]), .select(I0000_out), .\output (mem_cell_7_output), .in_4(clk),
    .Pin_Read(A0000[6]), .in_5(in_1));
  mem_cell mem_cell_8 (
    .\input (in_5[7]), .mode(in_4[0]), .select(I0000_out), .\output (mem_cell_8_output), .in_4(clk),
    .Pin_Read(A0000[7]), .in_5(in_1));
  and I0001 (I0001_out, not_2_out, not_4_out, not_1_out, in_3[0]);
  mem_cell mem_cell_9 (
    .\input (in_5[0]), .mode(in_4[0]), .select(I0001_out), .\output (mem_cell_9_output), .in_4(clk),
    .Pin_Read(A0001[0]), .in_5(in_1));
  mem_cell mem_cell_10 (
    .\input (in_5[1]), .mode(in_4[0]), .select(I0001_out), .\output (mem_cell_10_output), .in_4(clk),
    .Pin_Read(A0001[1]), .in_5(in_1));
  mem_cell mem_cell_11 (
    .\input (in_5[2]), .mode(in_4[0]), .select(I0001_out), .\output (mem_cell_11_output), .in_4(clk),
    .Pin_Read(A0001[2]), .in_5(in_1));
  mem_cell mem_cell_12 (
    .\input (in_5[3]), .mode(in_4[0]), .select(I0001_out), .\output (mem_cell_12_output), .in_4(clk),
    .Pin_Read(A0001[3]), .in_5(in_1));
  mem_cell mem_cell_13 (
    .\input (in_5[4]), .mode(in_4[0]), .select(I0001_out), .\output (mem_cell_13_output), .in_4(clk),
    .Pin_Read(A0001[4]), .in_5(in_1));
  mem_cell mem_cell_14 (
    .\input (in_5[5]), .mode(in_4[0]), .select(I0001_out), .\output (mem_cell_14_output), .in_4(clk),
    .Pin_Read(A0001[5]), .in_5(in_1));
  mem_cell mem_cell_15 (
    .\input (in_5[6]), .mode(in_4[0]), .select(I0001_out), .\output (mem_cell_15_output), .in_4(clk),
    .Pin_Read(A0001[6]), .in_5(in_1));
  mem_cell mem_cell_16 (
    .\input (in_5[7]), .mode(in_4[0]), .select(I0001_out), .\output (mem_cell_16_output), .in_4(clk),
    .Pin_Read(A0001[7]), .in_5(in_1));
  and I0010 (I0010_out, not_2_out, not_4_out, in_3[1], not_3_out);
  mem_cell mem_cell_17 (
    .\input (in_5[0]), .mode(in_4[0]), .select(I0010_out), .\output (mem_cell_17_output), .in_4(clk),
    .Pin_Read(A0010[0]), .in_5(in_1));
  mem_cell mem_cell_18 (
    .\input (in_5[1]), .mode(in_4[0]), .select(I0010_out), .\output (mem_cell_18_output), .in_4(clk),
    .Pin_Read(A0010[1]), .in_5(in_1));
  mem_cell mem_cell_19 (
    .\input (in_5[2]), .mode(in_4[0]), .select(I0010_out), .\output (mem_cell_19_output), .in_4(clk),
    .Pin_Read(A0010[2]), .in_5(in_1));
  mem_cell mem_cell_20 (
    .\input (in_5[3]), .mode(in_4[0]), .select(I0010_out), .\output (mem_cell_20_output), .in_4(clk),
    .Pin_Read(A0010[3]), .in_5(in_1));
  mem_cell mem_cell_21 (
    .\input (in_5[4]), .mode(in_4[0]), .select(I0010_out), .\output (mem_cell_21_output), .in_4(clk),
    .Pin_Read(A0010[4]), .in_5(in_1));
  mem_cell mem_cell_22 (
    .\input (in_5[5]), .mode(in_4[0]), .select(I0010_out), .\output (mem_cell_22_output), .in_4(clk),
    .Pin_Read(A0010[5]), .in_5(in_1));
  mem_cell mem_cell_23 (
    .\input (in_5[6]), .mode(in_4[0]), .select(I0010_out), .\output (mem_cell_23_output), .in_4(clk),
    .Pin_Read(A0010[6]), .in_5(in_1));
  mem_cell mem_cell_24 (
    .\input (in_5[7]), .mode(in_4[0]), .select(I0010_out), .\output (mem_cell_24_output), .in_4(clk),
    .Pin_Read(A0010[7]), .in_5(in_1));
  and I0011 (I0011_out, not_2_out, not_4_out, in_3[1], in_3[0]);
  mem_cell mem_cell_25 (
    .\input (in_5[0]), .mode(in_4[0]), .select(I0011_out), .\output (mem_cell_25_output), .in_4(clk),
    .Pin_Read(A0011[0]), .in_5(in_1));
  mem_cell mem_cell_26 (
    .\input (in_5[1]), .mode(in_4[0]), .select(I0011_out), .\output (mem_cell_26_output), .in_4(clk),
    .Pin_Read(A0011[1]), .in_5(in_1));
  mem_cell mem_cell_27 (
    .\input (in_5[2]), .mode(in_4[0]), .select(I0011_out), .\output (mem_cell_27_output), .in_4(clk),
    .Pin_Read(A0011[2]), .in_5(in_1));
  mem_cell mem_cell_28 (
    .\input (in_5[3]), .mode(in_4[0]), .select(I0011_out), .\output (mem_cell_28_output), .in_4(clk),
    .Pin_Read(A0011[3]), .in_5(in_1));
  mem_cell mem_cell_29 (
    .\input (in_5[4]), .mode(in_4[0]), .select(I0011_out), .\output (mem_cell_29_output), .in_4(clk),
    .Pin_Read(A0011[4]), .in_5(in_1));
  mem_cell mem_cell_30 (
    .\input (in_5[5]), .mode(in_4[0]), .select(I0011_out), .\output (mem_cell_30_output), .in_4(clk),
    .Pin_Read(A0011[5]), .in_5(in_1));
  mem_cell mem_cell_31 (
    .\input (in_5[6]), .mode(in_4[0]), .select(I0011_out), .\output (mem_cell_31_output), .in_4(clk),
    .Pin_Read(A0011[6]), .in_5(in_1));
  mem_cell mem_cell_32 (
    .\input (in_5[7]), .mode(in_4[0]), .select(I0011_out), .\output (mem_cell_32_output), .in_4(clk),
    .Pin_Read(A0011[7]), .in_5(in_1));
  and I0100 (I0100_out, not_2_out, in_3[2], not_1_out, not_3_out);
  or or_1 (or_1_out, mem_cell_1_output, mem_cell_9_output, mem_cell_17_output, mem_cell_25_output);
  or or_2 (or_2_out, mem_cell_2_output, mem_cell_10_output, mem_cell_18_output, mem_cell_26_output);
  or or_3 (or_3_out, mem_cell_3_output, mem_cell_11_output, mem_cell_19_output, mem_cell_27_output);
  or or_4 (or_4_out, mem_cell_4_output, mem_cell_12_output, mem_cell_20_output, mem_cell_28_output);
  or or_5 (or_5_out, mem_cell_5_output, mem_cell_13_output, mem_cell_21_output, mem_cell_29_output);
  or or_6 (or_6_out, mem_cell_6_output, mem_cell_14_output, mem_cell_22_output, mem_cell_30_output);
  or or_7 (or_7_out, mem_cell_7_output, mem_cell_15_output, mem_cell_23_output, mem_cell_31_output);
  or or_8 (or_8_out, mem_cell_8_output, mem_cell_16_output, mem_cell_24_output, mem_cell_32_output);
  mem_cell mem_cell_33 (
    .\input (in_5[0]), .mode(in_4[0]), .select(I0100_out), .\output (mem_cell_33_output), .in_4(clk),
    .Pin_Read(A0100[0]), .in_5(in_1));
  mem_cell mem_cell_34 (
    .\input (in_5[1]), .mode(in_4[0]), .select(I0100_out), .\output (mem_cell_34_output), .in_4(clk),
    .Pin_Read(A0100[1]), .in_5(in_1));
  mem_cell mem_cell_35 (
    .\input (in_5[2]), .mode(in_4[0]), .select(I0100_out), .\output (mem_cell_35_output), .in_4(clk),
    .Pin_Read(A0100[2]), .in_5(in_1));
  mem_cell mem_cell_36 (
    .\input (in_5[3]), .mode(in_4[0]), .select(I0100_out), .\output (mem_cell_36_output), .in_4(clk),
    .Pin_Read(A0100[3]), .in_5(in_1));
  mem_cell mem_cell_37 (
    .\input (in_5[4]), .mode(in_4[0]), .select(I0100_out), .\output (mem_cell_37_output), .in_4(clk),
    .Pin_Read(A0100[4]), .in_5(in_1));
  mem_cell mem_cell_38 (
    .\input (in_5[5]), .mode(in_4[0]), .select(I0100_out), .\output (mem_cell_38_output), .in_4(clk),
    .Pin_Read(A0100[5]), .in_5(in_1));
  mem_cell mem_cell_39 (
    .\input (in_5[6]), .mode(in_4[0]), .select(I0100_out), .\output (mem_cell_39_output), .in_4(clk),
    .Pin_Read(A0100[6]), .in_5(in_1));
  mem_cell mem_cell_40 (
    .\input (in_5[7]), .mode(in_4[0]), .select(I0100_out), .\output (mem_cell_40_output), .in_4(clk),
    .Pin_Read(A0100[7]), .in_5(in_1));
  and I0101 (I0101_out, not_2_out, in_3[2], not_1_out, in_3[0]);
  mem_cell mem_cell_41 (
    .\input (in_5[0]), .mode(in_4[0]), .select(I0101_out), .\output (mem_cell_41_output), .in_4(clk),
    .Pin_Read(A0101[0]), .in_5(in_1));
  mem_cell mem_cell_42 (
    .\input (in_5[1]), .mode(in_4[0]), .select(I0101_out), .\output (mem_cell_42_output), .in_4(clk),
    .Pin_Read(A0101[1]), .in_5(in_1));
  mem_cell mem_cell_43 (
    .\input (in_5[2]), .mode(in_4[0]), .select(I0101_out), .\output (mem_cell_43_output), .in_4(clk),
    .Pin_Read(A0101[2]), .in_5(in_1));
  mem_cell mem_cell_44 (
    .\input (in_5[3]), .mode(in_4[0]), .select(I0101_out), .\output (mem_cell_44_output), .in_4(clk),
    .Pin_Read(A0101[3]), .in_5(in_1));
  mem_cell mem_cell_45 (
    .\input (in_5[4]), .mode(in_4[0]), .select(I0101_out), .\output (mem_cell_45_output), .in_4(clk),
    .Pin_Read(A0101[4]), .in_5(in_1));
  mem_cell mem_cell_46 (
    .\input (in_5[5]), .mode(in_4[0]), .select(I0101_out), .\output (mem_cell_46_output), .in_4(clk),
    .Pin_Read(A0101[5]), .in_5(in_1));
  mem_cell mem_cell_47 (
    .\input (in_5[6]), .mode(in_4[0]), .select(I0101_out), .\output (mem_cell_47_output), .in_4(clk),
    .Pin_Read(A0101[6]), .in_5(in_1));
  mem_cell mem_cell_48 (
    .\input (in_5[7]), .mode(in_4[0]), .select(I0101_out), .\output (mem_cell_48_output), .in_4(clk),
    .Pin_Read(A0101[7]), .in_5(in_1));
  and I0110 (I0110_out, not_2_out, in_3[2], in_3[1], not_3_out);
  mem_cell mem_cell_49 (
    .\input (in_5[0]), .mode(in_4[0]), .select(I0110_out), .\output (mem_cell_49_output), .in_4(clk),
    .Pin_Read(A0110[0]), .in_5(in_1));
  mem_cell mem_cell_50 (
    .\input (in_5[1]), .mode(in_4[0]), .select(I0110_out), .\output (mem_cell_50_output), .in_4(clk),
    .Pin_Read(A0110[1]), .in_5(in_1));
  mem_cell mem_cell_51 (
    .\input (in_5[2]), .mode(in_4[0]), .select(I0110_out), .\output (mem_cell_51_output), .in_4(clk),
    .Pin_Read(A0110[2]), .in_5(in_1));
  mem_cell mem_cell_52 (
    .\input (in_5[3]), .mode(in_4[0]), .select(I0110_out), .\output (mem_cell_52_output), .in_4(clk),
    .Pin_Read(A0110[3]), .in_5(in_1));
  mem_cell mem_cell_53 (
    .\input (in_5[4]), .mode(in_4[0]), .select(I0110_out), .\output (mem_cell_53_output), .in_4(clk),
    .Pin_Read(A0110[4]), .in_5(in_1));
  mem_cell mem_cell_54 (
    .\input (in_5[5]), .mode(in_4[0]), .select(I0110_out), .\output (mem_cell_54_output), .in_4(clk),
    .Pin_Read(A0110[5]), .in_5(in_1));
  mem_cell mem_cell_55 (
    .\input (in_5[6]), .mode(in_4[0]), .select(I0110_out), .\output (mem_cell_55_output), .in_4(clk),
    .Pin_Read(A0110[6]), .in_5(in_1));
  mem_cell mem_cell_56 (
    .\input (in_5[7]), .mode(in_4[0]), .select(I0110_out), .\output (mem_cell_56_output), .in_4(clk),
    .Pin_Read(A0110[7]), .in_5(in_1));
  and I0111 (I0111_out, not_2_out, in_3[2], in_3[1], in_3[0]);
  mem_cell mem_cell_57 (
    .\input (in_5[0]), .mode(in_4[0]), .select(I0111_out), .\output (mem_cell_57_output), .in_4(clk),
    .Pin_Read(A0111[0]), .in_5(in_1));
  mem_cell mem_cell_58 (
    .\input (in_5[1]), .mode(in_4[0]), .select(I0111_out), .\output (mem_cell_58_output), .in_4(clk),
    .Pin_Read(A0111[1]), .in_5(in_1));
  mem_cell mem_cell_59 (
    .\input (in_5[2]), .mode(in_4[0]), .select(I0111_out), .\output (mem_cell_59_output), .in_4(clk),
    .Pin_Read(A0111[2]), .in_5(in_1));
  mem_cell mem_cell_60 (
    .\input (in_5[3]), .mode(in_4[0]), .select(I0111_out), .\output (mem_cell_60_output), .in_4(clk),
    .Pin_Read(A0111[3]), .in_5(in_1));
  mem_cell mem_cell_61 (
    .\input (in_5[4]), .mode(in_4[0]), .select(I0111_out), .\output (mem_cell_61_output), .in_4(clk),
    .Pin_Read(A0111[4]), .in_5(in_1));
  mem_cell mem_cell_62 (
    .\input (in_5[5]), .mode(in_4[0]), .select(I0111_out), .\output (mem_cell_62_output), .in_4(clk),
    .Pin_Read(A0111[5]), .in_5(in_1));
  mem_cell mem_cell_63 (
    .\input (in_5[6]), .mode(in_4[0]), .select(I0111_out), .\output (mem_cell_63_output), .in_4(clk),
    .Pin_Read(A0111[6]), .in_5(in_1));
  mem_cell mem_cell_64 (
    .\input (in_5[7]), .mode(in_4[0]), .select(I0111_out), .\output (mem_cell_64_output), .in_4(clk),
    .Pin_Read(A0111[7]), .in_5(in_1));
  or or_9 (or_9_out, mem_cell_33_output, mem_cell_41_output, or_1_out, mem_cell_49_output, mem_cell_57_output);
  or or_10 (or_10_out, mem_cell_34_output, mem_cell_42_output, or_2_out, mem_cell_50_output, mem_cell_58_output);
  or or_11 (or_11_out, mem_cell_35_output, mem_cell_43_output, or_3_out, mem_cell_51_output, mem_cell_59_output);
  or or_12 (or_12_out, mem_cell_36_output, mem_cell_44_output, or_4_out, mem_cell_52_output, mem_cell_60_output);
  or or_13 (or_13_out, mem_cell_37_output, mem_cell_45_output, or_5_out, mem_cell_53_output, mem_cell_61_output);
  or or_14 (or_14_out, mem_cell_38_output, mem_cell_46_output, or_6_out, mem_cell_54_output, mem_cell_62_output);
  or or_15 (or_15_out, mem_cell_39_output, mem_cell_47_output, or_7_out, mem_cell_55_output, mem_cell_63_output);
  or or_16 (or_16_out, mem_cell_40_output, mem_cell_48_output, or_8_out, mem_cell_56_output, mem_cell_64_output);
  and I1000 (I1000_out, in_3[3], not_4_out, not_1_out, not_3_out);
  mem_cell mem_cell_65 (
    .\input (in_5[0]), .mode(in_4[0]), .select(I1000_out), .\output (mem_cell_65_output), .in_4(clk),
    .Pin_Read(A1000[0]), .in_5(in_1));
  mem_cell mem_cell_66 (
    .\input (in_5[1]), .mode(in_4[0]), .select(I1000_out), .\output (mem_cell_66_output), .in_4(clk),
    .Pin_Read(A1000[1]), .in_5(in_1));
  mem_cell mem_cell_67 (
    .\input (in_5[2]), .mode(in_4[0]), .select(I1000_out), .\output (mem_cell_67_output), .in_4(clk),
    .Pin_Read(A1000[2]), .in_5(in_1));
  mem_cell mem_cell_68 (
    .\input (in_5[3]), .mode(in_4[0]), .select(I1000_out), .\output (mem_cell_68_output), .in_4(clk),
    .Pin_Read(A1000[3]), .in_5(in_1));
  mem_cell mem_cell_69 (
    .\input (in_5[4]), .mode(in_4[0]), .select(I1000_out), .\output (mem_cell_69_output), .in_4(clk),
    .Pin_Read(A1000[4]), .in_5(in_1));
  mem_cell mem_cell_70 (
    .\input (in_5[5]), .mode(in_4[0]), .select(I1000_out), .\output (mem_cell_70_output), .in_4(clk),
    .Pin_Read(A1000[5]), .in_5(in_1));
  mem_cell mem_cell_71 (
    .\input (in_5[6]), .mode(in_4[0]), .select(I1000_out), .\output (mem_cell_71_output), .in_4(clk),
    .Pin_Read(A1000[6]), .in_5(in_1));
  mem_cell mem_cell_72 (
    .\input (in_5[7]), .mode(in_4[0]), .select(I1000_out), .\output (mem_cell_72_output), .in_4(clk),
    .Pin_Read(A1000[7]), .in_5(in_1));
  and I1001 (I1001_out, in_3[3], not_4_out, not_1_out, in_3[0]);
  mem_cell mem_cell_73 (
    .\input (in_5[0]), .mode(in_4[0]), .select(I1001_out), .\output (mem_cell_73_output), .in_4(clk),
    .Pin_Read(A1001[0]), .in_5(in_1));
  mem_cell mem_cell_74 (
    .\input (in_5[1]), .mode(in_4[0]), .select(I1001_out), .\output (mem_cell_74_output), .in_4(clk),
    .Pin_Read(A1001[1]), .in_5(in_1));
  mem_cell mem_cell_75 (
    .\input (in_5[2]), .mode(in_4[0]), .select(I1001_out), .\output (mem_cell_75_output), .in_4(clk),
    .Pin_Read(A1001[2]), .in_5(in_1));
  mem_cell mem_cell_76 (
    .\input (in_5[3]), .mode(in_4[0]), .select(I1001_out), .\output (mem_cell_76_output), .in_4(clk),
    .Pin_Read(A1001[3]), .in_5(in_1));
  mem_cell mem_cell_77 (
    .\input (in_5[4]), .mode(in_4[0]), .select(I1001_out), .\output (mem_cell_77_output), .in_4(clk),
    .Pin_Read(A1001[4]), .in_5(in_1));
  mem_cell mem_cell_78 (
    .\input (in_5[5]), .mode(in_4[0]), .select(I1001_out), .\output (mem_cell_78_output), .in_4(clk),
    .Pin_Read(A1001[5]), .in_5(in_1));
  mem_cell mem_cell_79 (
    .\input (in_5[6]), .mode(in_4[0]), .select(I1001_out), .\output (mem_cell_79_output), .in_4(clk),
    .Pin_Read(A1001[6]), .in_5(in_1));
  mem_cell mem_cell_80 (
    .\input (in_5[7]), .mode(in_4[0]), .select(I1001_out), .\output (mem_cell_80_output), .in_4(clk),
    .Pin_Read(A1001[7]), .in_5(in_1));
  and I1010 (I1010_out, in_3[3], not_4_out, in_3[1], not_3_out);
  mem_cell mem_cell_81 (
    .\input (in_5[0]), .mode(in_4[0]), .select(I1010_out), .\output (mem_cell_81_output), .in_4(clk),
    .Pin_Read(A1010[0]), .in_5(in_1));
  mem_cell mem_cell_82 (
    .\input (in_5[1]), .mode(in_4[0]), .select(I1010_out), .\output (mem_cell_82_output), .in_4(clk),
    .Pin_Read(A1010[1]), .in_5(in_1));
  mem_cell mem_cell_83 (
    .\input (in_5[2]), .mode(in_4[0]), .select(I1010_out), .\output (mem_cell_83_output), .in_4(clk),
    .Pin_Read(A1010[2]), .in_5(in_1));
  mem_cell mem_cell_84 (
    .\input (in_5[3]), .mode(in_4[0]), .select(I1010_out), .\output (mem_cell_84_output), .in_4(clk),
    .Pin_Read(A1010[3]), .in_5(in_1));
  mem_cell mem_cell_85 (
    .\input (in_5[4]), .mode(in_4[0]), .select(I1010_out), .\output (mem_cell_85_output), .in_4(clk),
    .Pin_Read(A1010[4]), .in_5(in_1));
  mem_cell mem_cell_86 (
    .\input (in_5[5]), .mode(in_4[0]), .select(I1010_out), .\output (mem_cell_86_output), .in_4(clk),
    .Pin_Read(A1010[5]), .in_5(in_1));
  mem_cell mem_cell_87 (
    .\input (in_5[6]), .mode(in_4[0]), .select(I1010_out), .\output (mem_cell_87_output), .in_4(clk),
    .Pin_Read(A1010[6]), .in_5(in_1));
  mem_cell mem_cell_88 (
    .\input (in_5[7]), .mode(in_4[0]), .select(I1010_out), .\output (mem_cell_88_output), .in_4(clk),
    .Pin_Read(A1010[7]), .in_5(in_1));
  and I1011 (I1011_out, in_3[3], not_4_out, in_3[1], in_3[0]);
  mem_cell mem_cell_89 (
    .\input (in_5[0]), .mode(in_4[0]), .select(I1011_out), .\output (mem_cell_89_output), .in_4(clk),
    .Pin_Read(A1011[0]), .in_5(in_1));
  mem_cell mem_cell_90 (
    .\input (in_5[1]), .mode(in_4[0]), .select(I1011_out), .\output (mem_cell_90_output), .in_4(clk),
    .Pin_Read(A1011[1]), .in_5(in_1));
  mem_cell mem_cell_91 (
    .\input (in_5[2]), .mode(in_4[0]), .select(I1011_out), .\output (mem_cell_91_output), .in_4(clk),
    .Pin_Read(A1011[2]), .in_5(in_1));
  mem_cell mem_cell_92 (
    .\input (in_5[3]), .mode(in_4[0]), .select(I1011_out), .\output (mem_cell_92_output), .in_4(clk),
    .Pin_Read(A1011[3]), .in_5(in_1));
  mem_cell mem_cell_93 (
    .\input (in_5[4]), .mode(in_4[0]), .select(I1011_out), .\output (mem_cell_93_output), .in_4(clk),
    .Pin_Read(A1011[4]), .in_5(in_1));
  mem_cell mem_cell_94 (
    .\input (in_5[5]), .mode(in_4[0]), .select(I1011_out), .\output (mem_cell_94_output), .in_4(clk),
    .Pin_Read(A1011[5]), .in_5(in_1));
  mem_cell mem_cell_95 (
    .\input (in_5[6]), .mode(in_4[0]), .select(I1011_out), .\output (mem_cell_95_output), .in_4(clk),
    .Pin_Read(A1011[6]), .in_5(in_1));
  mem_cell mem_cell_96 (
    .\input (in_5[7]), .mode(in_4[0]), .select(I1011_out), .\output (mem_cell_96_output), .in_4(clk),
    .Pin_Read(A1011[7]), .in_5(in_1));
  and I1100 (I1100_out, in_3[3], in_3[2], not_1_out, not_3_out);
  or or_17 (or_17_out, mem_cell_65_output, mem_cell_73_output, or_9_out, mem_cell_81_output, mem_cell_89_output);
  or or_18 (or_18_out, mem_cell_66_output, mem_cell_74_output, or_10_out, mem_cell_82_output, mem_cell_90_output);
  or or_19 (or_19_out, mem_cell_67_output, mem_cell_75_output, or_11_out, mem_cell_83_output, mem_cell_91_output);
  or or_20 (or_20_out, mem_cell_68_output, mem_cell_76_output, or_12_out, mem_cell_84_output, mem_cell_92_output);
  or or_21 (or_21_out, mem_cell_69_output, mem_cell_77_output, or_13_out, mem_cell_85_output, mem_cell_93_output);
  or or_22 (or_22_out, mem_cell_70_output, mem_cell_78_output, or_14_out, mem_cell_86_output, mem_cell_94_output);
  or or_23 (or_23_out, mem_cell_71_output, mem_cell_79_output, or_15_out, mem_cell_87_output, mem_cell_95_output);
  or or_24 (or_24_out, mem_cell_72_output, mem_cell_80_output, or_16_out, mem_cell_88_output, mem_cell_96_output);
  mem_cell mem_cell_97 (
    .\input (in_5[0]), .mode(in_4[0]), .select(I1100_out), .\output (mem_cell_97_output), .in_4(clk),
    .Pin_Read(A1100[0]), .in_5(in_1));
  mem_cell mem_cell_98 (
    .\input (in_5[1]), .mode(in_4[0]), .select(I1100_out), .\output (mem_cell_98_output), .in_4(clk),
    .Pin_Read(A1100[1]), .in_5(in_1));
  mem_cell mem_cell_99 (
    .\input (in_5[2]), .mode(in_4[0]), .select(I1100_out), .\output (mem_cell_99_output), .in_4(clk),
    .Pin_Read(A1100[2]), .in_5(in_1));
  mem_cell mem_cell_100 (
    .\input (in_5[3]), .mode(in_4[0]), .select(I1100_out), .\output (mem_cell_100_output), .in_4(clk),
    .Pin_Read(A1100[3]), .in_5(in_1));
  mem_cell mem_cell_101 (
    .\input (in_5[4]), .mode(in_4[0]), .select(I1100_out), .\output (mem_cell_101_output), .in_4(clk),
    .Pin_Read(A1100[4]), .in_5(in_1));
  mem_cell mem_cell_102 (
    .\input (in_5[5]), .mode(in_4[0]), .select(I1100_out), .\output (mem_cell_102_output), .in_4(clk),
    .Pin_Read(A1100[5]), .in_5(in_1));
  mem_cell mem_cell_103 (
    .\input (in_5[6]), .mode(in_4[0]), .select(I1100_out), .\output (mem_cell_103_output), .in_4(clk),
    .Pin_Read(A1100[6]), .in_5(in_1));
  mem_cell mem_cell_104 (
    .\input (in_5[7]), .mode(in_4[0]), .select(I1100_out), .\output (mem_cell_104_output), .in_4(clk),
    .Pin_Read(A1100[7]), .in_5(in_1));
  and I1101 (I1101_out, in_3[3], in_3[2], not_1_out, in_3[0]);
  mem_cell mem_cell_105 (
    .\input (in_5[0]), .mode(in_4[0]), .select(I1101_out), .\output (mem_cell_105_output), .in_4(clk),
    .Pin_Read(A1101[0]), .in_5(in_1));
  mem_cell mem_cell_106 (
    .\input (in_5[1]), .mode(in_4[0]), .select(I1101_out), .\output (mem_cell_106_output), .in_4(clk),
    .Pin_Read(A1101[1]), .in_5(in_1));
  mem_cell mem_cell_107 (
    .\input (in_5[2]), .mode(in_4[0]), .select(I1101_out), .\output (mem_cell_107_output), .in_4(clk),
    .Pin_Read(A1101[2]), .in_5(in_1));
  mem_cell mem_cell_108 (
    .\input (in_5[3]), .mode(in_4[0]), .select(I1101_out), .\output (mem_cell_108_output), .in_4(clk),
    .Pin_Read(A1101[3]), .in_5(in_1));
  mem_cell mem_cell_109 (
    .\input (in_5[4]), .mode(in_4[0]), .select(I1101_out), .\output (mem_cell_109_output), .in_4(clk),
    .Pin_Read(A1101[4]), .in_5(in_1));
  mem_cell mem_cell_110 (
    .\input (in_5[5]), .mode(in_4[0]), .select(I1101_out), .\output (mem_cell_110_output), .in_4(clk),
    .Pin_Read(A1101[5]), .in_5(in_1));
  mem_cell mem_cell_111 (
    .\input (in_5[6]), .mode(in_4[0]), .select(I1101_out), .\output (mem_cell_111_output), .in_4(clk),
    .Pin_Read(A1101[6]), .in_5(in_1));
  mem_cell mem_cell_112 (
    .\input (in_5[7]), .mode(in_4[0]), .select(I1101_out), .\output (mem_cell_112_output), .in_4(clk),
    .Pin_Read(A1101[7]), .in_5(in_1));
  and I1110 (I1110_out, in_3[3], in_3[2], in_3[1], not_3_out);
  mem_cell mem_cell_113 (
    .\input (in_5[0]), .mode(in_4[0]), .select(I1110_out), .\output (mem_cell_113_output), .in_4(clk),
    .Pin_Read(A1110[0]), .in_5(in_1));
  mem_cell mem_cell_114 (
    .\input (in_5[1]), .mode(in_4[0]), .select(I1110_out), .\output (mem_cell_114_output), .in_4(clk),
    .Pin_Read(A1110[1]), .in_5(in_1));
  mem_cell mem_cell_115 (
    .\input (in_5[2]), .mode(in_4[0]), .select(I1110_out), .\output (mem_cell_115_output), .in_4(clk),
    .Pin_Read(A1110[2]), .in_5(in_1));
  mem_cell mem_cell_116 (
    .\input (in_5[3]), .mode(in_4[0]), .select(I1110_out), .\output (mem_cell_116_output), .in_4(clk),
    .Pin_Read(A1110[3]), .in_5(in_1));
  mem_cell mem_cell_117 (
    .\input (in_5[4]), .mode(in_4[0]), .select(I1110_out), .\output (mem_cell_117_output), .in_4(clk),
    .Pin_Read(A1110[4]), .in_5(in_1));
  mem_cell mem_cell_118 (
    .\input (in_5[5]), .mode(in_4[0]), .select(I1110_out), .\output (mem_cell_118_output), .in_4(clk),
    .Pin_Read(A1110[5]), .in_5(in_1));
  mem_cell mem_cell_119 (
    .\input (in_5[6]), .mode(in_4[0]), .select(I1110_out), .\output (mem_cell_119_output), .in_4(clk),
    .Pin_Read(A1110[6]), .in_5(in_1));
  mem_cell mem_cell_120 (
    .\input (in_5[7]), .mode(in_4[0]), .select(I1110_out), .\output (mem_cell_120_output), .in_4(clk),
    .Pin_Read(A1110[7]), .in_5(in_1));
  and I111 (I111_out, in_3[3], in_3[2], in_3[1], in_3[0]);
  mem_cell mem_cell_121 (
    .\input (in_5[0]), .mode(in_4[0]), .select(I111_out), .\output (mem_cell_121_output), .in_4(clk),
    .Pin_Read(A1111[0]), .in_5(in_1));
  mem_cell mem_cell_122 (
    .\input (in_5[1]), .mode(in_4[0]), .select(I111_out), .\output (mem_cell_122_output), .in_4(clk),
    .Pin_Read(A1111[1]), .in_5(in_1));
  mem_cell mem_cell_123 (
    .\input (in_5[2]), .mode(in_4[0]), .select(I111_out), .\output (mem_cell_123_output), .in_4(clk),
    .Pin_Read(A1111[2]), .in_5(in_1));
  mem_cell mem_cell_124 (
    .\input (in_5[3]), .mode(in_4[0]), .select(I111_out), .\output (mem_cell_124_output), .in_4(clk),
    .Pin_Read(A1111[3]), .in_5(in_1));
  mem_cell mem_cell_125 (
    .\input (in_5[4]), .mode(in_4[0]), .select(I111_out), .\output (mem_cell_125_output), .in_4(clk),
    .Pin_Read(A1111[4]), .in_5(in_1));
  mem_cell mem_cell_126 (
    .\input (in_5[5]), .mode(in_4[0]), .select(I111_out), .\output (mem_cell_126_output), .in_4(clk),
    .Pin_Read(A1111[5]), .in_5(in_1));
  mem_cell mem_cell_127 (
    .\input (in_5[6]), .mode(in_4[0]), .select(I111_out), .\output (mem_cell_127_output), .in_4(clk),
    .Pin_Read(A1111[6]), .in_5(in_1));
  mem_cell mem_cell_128 (
    .\input (in_5[7]), .mode(in_4[0]), .select(I111_out), .\output (mem_cell_128_output), .in_4(clk),
    .Pin_Read(A1111[7]), .in_5(in_1));
  or or_25 (data_output[0], mem_cell_97_output, mem_cell_105_output, or_17_out, mem_cell_113_output, mem_cell_121_output);
  or or_26 (data_output[1], mem_cell_98_output, mem_cell_106_output, or_18_out, mem_cell_114_output, mem_cell_122_output);
  or or_27 (data_output[2], mem_cell_99_output, mem_cell_107_output, or_19_out, mem_cell_115_output, mem_cell_123_output);
  or or_28 (data_output[3], mem_cell_100_output, mem_cell_108_output, or_20_out, mem_cell_116_output, mem_cell_124_output);
  or or_29 (data_output[4], mem_cell_101_output, mem_cell_109_output, or_21_out, mem_cell_117_output, mem_cell_125_output);
  or or_30 (data_output[5], mem_cell_102_output, mem_cell_110_output, or_22_out, mem_cell_118_output, mem_cell_126_output);
  or or_31 (data_output[6], mem_cell_103_output, mem_cell_111_output, or_23_out, mem_cell_119_output, mem_cell_127_output);
  or or_32 (data_output[7], mem_cell_104_output, mem_cell_112_output, or_24_out, mem_cell_120_output, mem_cell_128_output);

  // Notes on the sheet:
  //   address input
  //   data input
  //   address space
  //   mode input 
  //   data space
  //   RAM
endmodule

module MODE_REG (
  input  I,
  input  in_2,
  output [7:0] O
);

  wire and_1_out, not_1_out, not_2_out, not_3_out, not_4_out;

  not not_1 (not_1_out, not_2_out);
  not not_2 (not_2_out, I);
  not not_3 (not_3_out, not_4_out);
  not not_4 (not_4_out, in_2);
  D_Flip_Flop #(.trigger("high")) d_ff_1 (.D(not_1_out), .clk(and_1_out), .Q(O[0]));  // open: Qn, preset, reset
  and and_1 (and_1_out, not_3_out, in_2);

  assign O[7:1] = {7{1'b0}};
endmodule

module GENERAL_REG (
  input  in_1,
  input  [7:0] I,
  input  in_3,
  output [7:0] O
);

  wire and_1_out, not_1_out, not_2_out;

  not not_1 (not_1_out, in_1);
  not not_2 (not_2_out, not_1_out);
  and and_1 (and_1_out, in_1, not_2_out);
  D_Flip_Flop #(.trigger("high")) d_ff_1 (.D(I[0]), .clk(and_1_out), .Q(O[0]), .reset(in_3));  // open: Qn, preset
  D_Flip_Flop #(.trigger("high")) d_ff_2 (.D(I[1]), .clk(and_1_out), .Q(O[1]), .reset(in_3));  // open: Qn, preset
  D_Flip_Flop #(.trigger("high")) d_ff_3 (.D(I[2]), .clk(and_1_out), .Q(O[2]), .reset(in_3));  // open: Qn, preset
  D_Flip_Flop #(.trigger("high")) d_ff_4 (.D(I[3]), .clk(and_1_out), .Q(O[3]), .reset(in_3));  // open: Qn, preset
  D_Flip_Flop #(.trigger("high")) d_ff_5 (.D(I[4]), .clk(and_1_out), .Q(O[4]), .reset(in_3));  // open: Qn, preset
  D_Flip_Flop #(.trigger("high")) d_ff_6 (.D(I[5]), .clk(and_1_out), .Q(O[5]), .reset(in_3));  // open: Qn, preset
  D_Flip_Flop #(.trigger("high")) d_ff_7 (.D(I[6]), .clk(and_1_out), .Q(O[6]), .reset(in_3));  // open: Qn, preset
  D_Flip_Flop #(.trigger("high")) d_ff_8 (.D(I[7]), .clk(and_1_out), .Q(O[7]), .reset(in_3));  // open: Qn, preset
  T_Flip_Flop t_ff_1 (.T(1'b1), .clk(and_1_out), .reset(in_3));  // open: Q, Qn, preset
endmodule

module INCBY1 (
  input  [7:0] from_PC,
  input  Inc,
  output [7:0] to_PC
);

  wire and_1_out, and_2_out, and_3_out, and_4_out, and_5_out, and_6_out, and_7_out;
  wire [7:0] general_reg_1_o;

  GENERAL_REG general_reg_1 (.O(general_reg_1_o), .I(from_PC), .in_1(Inc));  // open: in_3
  // Probe on general_reg_1_o
  xor xor_1 (to_PC[0], general_reg_1_o[0], 1'b1);
  and and_1 (and_1_out, general_reg_1_o[0], 1'b1);
  xor xor_2 (to_PC[1], and_1_out, general_reg_1_o[1]);
  and and_2 (and_2_out, and_1_out, general_reg_1_o[1]);
  xor xor_3 (to_PC[2], and_2_out, general_reg_1_o[2]);
  and and_3 (and_3_out, and_2_out, general_reg_1_o[2]);
  xor xor_4 (to_PC[3], and_3_out, general_reg_1_o[3]);
  and and_4 (and_4_out, and_3_out, general_reg_1_o[3]);
  xor xor_5 (to_PC[4], and_4_out, general_reg_1_o[4]);
  and and_5 (and_5_out, and_4_out, general_reg_1_o[4]);
  xor xor_6 (to_PC[5], and_5_out, general_reg_1_o[5]);
  and and_6 (and_6_out, and_5_out, general_reg_1_o[5]);
  xor xor_7 (to_PC[6], and_6_out, general_reg_1_o[6]);
  and and_7 (and_7_out, and_6_out, general_reg_1_o[6]);
  xor xor_8 (to_PC[7], and_7_out, general_reg_1_o[7]);
  // AND_Gate and_8 has open pins: in0=and_7_out, in1=general_reg_1_o[7], out=open
endmodule

module add1bit (
  input  in_1,
  input  in_2,
  input  in_3,
  output out_4,
  output out_5
);

  wire and_1_out, and_2_out, xor_1_out;

  xor xor_1 (xor_1_out, in_2, in_3);
  and and_1 (and_1_out, in_1, xor_1_out);
  and and_2 (and_2_out, in_2, in_3);
  xor xor_2 (out_4, in_1, xor_1_out);
  or or_1 (out_5, and_1_out, and_2_out);
endmodule

module ALU (
  input  Mode,
  input  [7:0] L,
  input  ALU_ACTV,
  input  L_W,
  input  [7:0] R,
  input  R_W,
  input  in_7,
  output [7:0] O,
  output [7:0] Flags
);

  wire and_1_out, full_adder_1_out_5, full_adder_2_out_5, full_adder_3_out_5, full_adder_4_out_5,
       full_adder_5_out_5, full_adder_6_out_5, full_adder_7_out_5, not_1_out, not_2_out, not_3_out,
       not_4_out, not_5_out, not_6_out, not_7_out, not_8_out, not_9_out;
  wire [2:0] and_3_out;
  wire [7:0] LEFT_REGISTER_o, RIGHT_REGISTER_o, twos_comp_converter_1_out_3, xor_1_out;

  // Probe on L
  // Probe on R
  TWOS_COMP_CONVERTER twos_comp_converter_1 (.out_3(twos_comp_converter_1_out_3), .in_2(LEFT_REGISTER_o), .in_1(Mode));
  // Probe on LEFT_REGISTER_o
  GENERAL_REG LEFT_REGISTER (.O(LEFT_REGISTER_o), .I(L), .in_1(L_W), .in_3(in_7));
  // Probe on RIGHT_REGISTER_o
  GENERAL_REG RIGHT_REGISTER (.O(RIGHT_REGISTER_o), .I(R), .in_1(R_W), .in_3(in_7));
  xor xor_1 (xor_1_out[0], twos_comp_converter_1_out_3[0], RIGHT_REGISTER_o[0]);
  and and_1 (and_1_out, twos_comp_converter_1_out_3[0], RIGHT_REGISTER_o[0]);
  FULL_ADDER full_adder_1 (
    .out_5(full_adder_1_out_5), .B(twos_comp_converter_1_out_3[1]), .Carry_In(RIGHT_REGISTER_o[1]),
    .A(and_1_out), .Sum(xor_1_out[1]));
  FULL_ADDER full_adder_2 (
    .out_5(full_adder_2_out_5), .B(twos_comp_converter_1_out_3[2]), .Carry_In(RIGHT_REGISTER_o[2]),
    .A(full_adder_1_out_5), .Sum(xor_1_out[2]));
  FULL_ADDER full_adder_3 (
    .out_5(full_adder_3_out_5), .B(twos_comp_converter_1_out_3[3]), .Carry_In(RIGHT_REGISTER_o[3]),
    .A(full_adder_2_out_5), .Sum(xor_1_out[3]));
  FULL_ADDER full_adder_4 (
    .out_5(full_adder_4_out_5), .B(twos_comp_converter_1_out_3[4]), .Carry_In(RIGHT_REGISTER_o[4]),
    .A(full_adder_3_out_5), .Sum(xor_1_out[4]));
  FULL_ADDER full_adder_5 (
    .out_5(full_adder_5_out_5), .B(twos_comp_converter_1_out_3[5]), .Carry_In(RIGHT_REGISTER_o[5]),
    .A(full_adder_4_out_5), .Sum(xor_1_out[5]));
  FULL_ADDER full_adder_6 (
    .out_5(full_adder_6_out_5), .B(twos_comp_converter_1_out_3[6]), .Carry_In(RIGHT_REGISTER_o[6]),
    .A(full_adder_5_out_5), .Sum(xor_1_out[6]));
  FULL_ADDER full_adder_7 (
    .out_5(full_adder_7_out_5), .B(twos_comp_converter_1_out_3[7]), .Carry_In(RIGHT_REGISTER_o[7]),
    .A(full_adder_6_out_5), .Sum(xor_1_out[7]));
  not not_1 (not_1_out, Mode);
  and and_2 (and_3_out[2], not_1_out, full_adder_7_out_5);
  not not_2 (not_2_out, xor_1_out[0]);
  not not_3 (not_3_out, xor_1_out[1]);
  not not_4 (not_4_out, xor_1_out[2]);
  not not_5 (not_5_out, xor_1_out[3]);
  and and_3 (and_3_out[0], not_2_out, not_3_out, not_4_out, not_5_out, not_6_out, not_7_out, not_8_out, not_9_out);
  not not_6 (not_6_out, xor_1_out[4]);
  not not_7 (not_7_out, xor_1_out[5]);
  not not_8 (not_8_out, xor_1_out[6]);
  not not_9 (not_9_out, xor_1_out[7]);
  and and_4 (and_3_out[1], Mode, xor_1_out[7]);
  GENERAL_REG A_REGISTER (.O(O), .I(xor_1_out), .in_1(ALU_ACTV), .in_3(in_7));
  GENERAL_REG general_reg_1 (.O(Flags), .I({{5{1'b0}}, and_3_out}), .in_1(ALU_ACTV), .in_3(in_7));
  // Probe on O

  // Notes on the sheet:
  //   Clock
  //   010 = NEGATIVE
  //   001 = ZERO
  //   100 = OVERFLOW
endmodule

module FULL_ADDER (
  input  A,
  input  B,
  input  Carry_In,
  output Sum,
  output out_5
);

  wire and_1_out, and_2_out, xor_1_out;

  xor xor_1 (xor_1_out, A, B);
  xor xor_2 (Sum, xor_1_out, Carry_In);
  and and_1 (and_1_out, xor_1_out, Carry_In);
  and and_2 (and_2_out, A, B);
  or or_1 (out_5, and_1_out, and_2_out);

  // Notes on the sheet:
  //   Carry_Out
endmodule

module TWOS_COMP_CONVERTER (
  input  in_1,
  input  [7:0] in_2,
  output [7:0] out_3
);

  wire and_1_out, and_2_out, and_3_out, and_4_out, and_5_out, and_6_out, and_7_out, xor_1_out, xor_2_out,
       xor_3_out, xor_4_out, xor_5_out, xor_6_out, xor_7_out, xor_8_out;

  xor xor_1 (xor_1_out, in_2[0], in_1);
  xor xor_2 (xor_2_out, in_2[1], in_1);
  xor xor_3 (xor_3_out, in_2[2], in_1);
  xor xor_4 (xor_4_out, in_2[3], in_1);
  xor xor_5 (xor_5_out, in_2[4], in_1);
  xor xor_6 (xor_6_out, in_2[5], in_1);
  xor xor_7 (xor_7_out, in_2[6], in_1);
  xor xor_8 (xor_8_out, in_2[7], in_1);
  xor xor_9 (out_3[0], xor_1_out, in_1);
  and and_1 (and_1_out, xor_1_out, in_1);
  and and_2 (and_2_out, and_1_out, xor_2_out);
  xor xor_10 (out_3[1], and_1_out, xor_2_out);
  xor xor_11 (out_3[2], and_2_out, xor_3_out);
  and and_3 (and_3_out, and_2_out, xor_3_out);
  xor xor_12 (out_3[3], and_3_out, xor_4_out);
  and and_4 (and_4_out, and_3_out, xor_4_out);
  and and_5 (and_5_out, and_4_out, xor_5_out);
  xor xor_13 (out_3[4], and_4_out, xor_5_out);
  xor xor_14 (out_3[5], and_5_out, xor_6_out);
  and and_6 (and_6_out, and_5_out, xor_6_out);
  xor xor_15 (out_3[6], and_6_out, xor_7_out);
  and and_7 (and_7_out, and_6_out, xor_7_out);
  xor xor_16 (out_3[7], and_7_out, xor_8_out);
endmodule

module INPUT_BUFFER (
  input  in_1,
  input  in_2,
  input  in_3,
  input  in_4,
  input  in_5,
  input  in_6,
  input  in_7,
  input  in_8,
  input  in_9,
  input  in_10,
  output [7:0] out_11
);

  Priority_Encoder #(.select(4)) priority_encoder_1 (
    .in0(in_1), .in1(in_2), .in2(in_3), .in3(in_4), .in4(in_5), .in5(in_6), .in6(in_7), .in7(in_8),
    .in8(in_9), .in9(in_10), .in10(1'b0), .in11(1'b0), .in12(1'b0), .in13(1'b0), .in14(1'b0), .in15(1'b0),
    .out(out_11[3:0]));  // open: gs, en_out, en_in

  assign out_11[7:4] = 4'b0000;
endmodule

module DISP_HELP_THREE_SHIFT (
  input  in_1,
  input  in_2,
  input  in_3,
  input  in_4,
  output out_5,
  output out_6,
  output out_7,
  output out_8
);

  wire adder_1_cout, adder_2_cout, adder_3_cout, and_1_out, and_2_out, or_1_out;

  and and_1 (and_1_out, in_1, in_3);
  and and_2 (and_2_out, in_2, in_3);
  or or_1 (or_1_out, and_1_out, and_2_out, in_4);
  Adder #(.width(1)) adder_1 (.a(in_1), .b(or_1_out), .out(out_5), .cout(adder_1_cout));  // open: cin
  Adder #(.width(1)) adder_2 (.a(adder_1_cout), .b(in_2), .out(out_6), .cin(or_1_out), .cout(adder_2_cout));
  Adder #(.width(1)) adder_3 (.a(adder_2_cout), .b(in_3), .out(out_7), .cout(adder_3_cout));  // open: cin
  Adder #(.width(1)) adder_4 (.a(adder_3_cout), .b(in_4), .out(out_8));  // open: cin, cout
endmodule

module DISPLAY (
  input  [7:0] in_1,
  output [6:0] out_2,
  output [6:0] out_3,
  output [6:0] out_4
);

  wire decoder_1_out0, decoder_1_out1, decoder_1_out2, decoder_1_out3, decoder_1_out4, decoder_1_out5,
       decoder_1_out6, decoder_1_out7, decoder_1_out8, decoder_1_out9, decoder_1_out10, decoder_1_out11,
       decoder_1_out12, decoder_1_out13, decoder_1_out14, decoder_1_out15, decoder_2_out0, decoder_2_out1,
       decoder_2_out2, decoder_2_out3, decoder_2_out4, decoder_2_out5, decoder_2_out6, decoder_2_out7,
       decoder_2_out8, decoder_2_out9, decoder_2_out10, decoder_2_out11, decoder_2_out12, decoder_2_out13,
       decoder_2_out14, decoder_2_out15, decoder_3_out0, decoder_3_out1, decoder_3_out2, decoder_3_out3,
       decoder_3_out4, decoder_3_out5, decoder_3_out6, decoder_3_out7, decoder_3_out8, decoder_3_out9,
       decoder_3_out10, decoder_3_out11, decoder_3_out12, decoder_3_out13, decoder_3_out14, decoder_3_out15,
       disp_help_three_shift_1_out_5, disp_help_three_shift_1_out_6, disp_help_three_shift_1_out_7,
       disp_help_three_shift_1_out_8, disp_help_three_shift_2_out_5, disp_help_three_shift_2_out_6,
       disp_help_three_shift_2_out_7, disp_help_three_shift_2_out_8, disp_help_three_shift_3_out_5,
       disp_help_three_shift_3_out_6, disp_help_three_shift_3_out_7, disp_help_three_shift_3_out_8,
       disp_help_three_shift_4_out_5, disp_help_three_shift_4_out_6, disp_help_three_shift_4_out_7,
       disp_help_three_shift_5_out_5, disp_help_three_shift_5_out_6, disp_help_three_shift_5_out_7,
       disp_help_three_shift_5_out_8, not_1_out, not_2_out, not_3_out, not_4_out, not_5_out, not_6_out,
       not_7_out, not_8_out, not_10_out, not_11_out, not_12_out, not_13_out, not_14_out, not_15_out,
       not_16_out, not_17_out, not_18_out, not_19_out, not_20_out, not_22_out, not_23_out, not_24_out,
       not_25_out, not_26_out, not_27_out, not_28_out, not_29_out, not_30_out, not_31_out, not_32_out,
       not_33_out, not_34_out, not_35_out, not_36_out, not_37_out, not_38_out, not_39_out, not_40_out,
       not_41_out, not_42_out, not_43_out, not_44_out, not_45_out, not_46_out, not_47_out;
  wire [1:0] disp_help_three_shift_6_out_8;
  wire [3:0] disp_help_three_shift_7_out_8;
  wire [3:1] disp_help_three_shift_7_out_5;

  DISP_HELP_THREE_SHIFT disp_help_three_shift_1 (
    .in_1(in_1[5]), .out_5(disp_help_three_shift_1_out_5), .in_2(in_1[6]),
    .out_6(disp_help_three_shift_1_out_6), .out_7(disp_help_three_shift_1_out_7), .in_3(in_1[7]),
    .out_8(disp_help_three_shift_1_out_8), .in_4(1'b0));
  DISP_HELP_THREE_SHIFT disp_help_three_shift_2 (
    .in_1(in_1[4]), .out_5(disp_help_three_shift_2_out_5), .in_2(disp_help_three_shift_1_out_5),
    .out_6(disp_help_three_shift_2_out_6), .out_7(disp_help_three_shift_2_out_7),
    .in_3(disp_help_three_shift_1_out_6), .out_8(disp_help_three_shift_2_out_8),
    .in_4(disp_help_three_shift_1_out_7));
  DISP_HELP_THREE_SHIFT disp_help_three_shift_3 (
    .in_1(in_1[3]), .out_5(disp_help_three_shift_3_out_5), .in_2(disp_help_three_shift_2_out_5),
    .out_6(disp_help_three_shift_3_out_6), .out_7(disp_help_three_shift_3_out_7),
    .in_3(disp_help_three_shift_2_out_6), .out_8(disp_help_three_shift_3_out_8),
    .in_4(disp_help_three_shift_2_out_7));
  DISP_HELP_THREE_SHIFT disp_help_three_shift_4 (
    .in_1(disp_help_three_shift_3_out_8), .out_5(disp_help_three_shift_4_out_5),
    .in_2(disp_help_three_shift_2_out_8), .out_6(disp_help_three_shift_4_out_6),
    .out_7(disp_help_three_shift_4_out_7), .in_3(disp_help_three_shift_1_out_8),
    .out_8(disp_help_three_shift_6_out_8[1]), .in_4(1'b0));
  DISP_HELP_THREE_SHIFT disp_help_three_shift_5 (
    .in_1(in_1[2]), .out_5(disp_help_three_shift_5_out_5), .in_2(disp_help_three_shift_3_out_5),
    .out_6(disp_help_three_shift_5_out_6), .out_7(disp_help_three_shift_5_out_7),
    .in_3(disp_help_three_shift_3_out_6), .out_8(disp_help_three_shift_5_out_8),
    .in_4(disp_help_three_shift_3_out_7));
  DISP_HELP_THREE_SHIFT disp_help_three_shift_6 (
    .in_1(disp_help_three_shift_5_out_8), .out_5(disp_help_three_shift_7_out_8[1]),
    .in_2(disp_help_three_shift_4_out_5), .out_6(disp_help_three_shift_7_out_8[2]),
    .out_7(disp_help_three_shift_7_out_8[3]), .in_3(disp_help_three_shift_4_out_6),
    .out_8(disp_help_three_shift_6_out_8[0]), .in_4(disp_help_three_shift_4_out_7));
  DISP_HELP_THREE_SHIFT disp_help_three_shift_7 (
    .in_1(in_1[1]), .out_5(disp_help_three_shift_7_out_5[1]), .in_2(disp_help_three_shift_5_out_5),
    .out_6(disp_help_three_shift_7_out_5[2]), .out_7(disp_help_three_shift_7_out_5[3]),
    .in_3(disp_help_three_shift_5_out_6), .out_8(disp_help_three_shift_7_out_8[0]),
    .in_4(disp_help_three_shift_5_out_7));
  Decoder #(.select(4), .enable("false")) decoder_1 (
    .out0(decoder_1_out0), .out1(decoder_1_out1), .out2(decoder_1_out2), .out3(decoder_1_out3),
    .out4(decoder_1_out4), .out5(decoder_1_out5), .out6(decoder_1_out6), .out7(decoder_1_out7),
    .out8(decoder_1_out8), .out9(decoder_1_out9), .out10(decoder_1_out10), .out11(decoder_1_out11),
    .out12(decoder_1_out12), .out13(decoder_1_out13), .out14(decoder_1_out14), .out15(decoder_1_out15),
    .sel({disp_help_three_shift_7_out_5, in_1[0]}));
  not not_1 (not_1_out, decoder_1_out1);
  not not_2 (not_2_out, decoder_1_out4);
  not not_3 (not_3_out, decoder_1_out9);
  not not_4 (not_4_out, decoder_1_out7);
  not not_5 (not_5_out, decoder_1_out1);
  and and_1 (out_4[0], not_5_out, not_6_out);
  not not_6 (not_6_out, decoder_1_out4);
  not not_7 (not_7_out, decoder_1_out5);
  and and_2 (out_4[1], not_7_out, not_8_out);
  not not_8 (not_8_out, decoder_1_out6);
  not not_9 (out_4[2], decoder_1_out2);
  and and_3 (out_4[3], not_1_out, not_2_out, not_3_out, not_4_out);
  or or_1 (out_4[4], decoder_1_out2, decoder_1_out0, decoder_1_out6, decoder_1_out8);
  not not_10 (not_10_out, decoder_1_out1);
  not not_11 (not_11_out, decoder_1_out2);
  and and_4 (out_4[5], not_10_out, not_11_out, not_12_out, not_13_out);
  not not_12 (not_12_out, decoder_1_out7);
  not not_13 (not_13_out, decoder_1_out3);
  not not_14 (not_14_out, decoder_1_out0);
  not not_15 (not_15_out, decoder_1_out1);
  and and_5 (out_4[6], not_14_out, not_15_out, not_16_out);
  not not_16 (not_16_out, decoder_1_out7);
  Decoder #(.select(4), .enable("false")) decoder_2 (
    .out0(decoder_2_out0), .out1(decoder_2_out1), .out2(decoder_2_out2), .out3(decoder_2_out3),
    .out4(decoder_2_out4), .out5(decoder_2_out5), .out6(decoder_2_out6), .out7(decoder_2_out7),
    .out8(decoder_2_out8), .out9(decoder_2_out9), .out10(decoder_2_out10), .out11(decoder_2_out11),
    .out12(decoder_2_out12), .out13(decoder_2_out13), .out14(decoder_2_out14), .out15(decoder_2_out15),
    .sel(disp_help_three_shift_7_out_8));
  not not_17 (not_17_out, decoder_2_out1);
  and and_6 (out_3[0], not_17_out, not_18_out);
  not not_18 (not_18_out, decoder_2_out4);
  not not_19 (not_19_out, decoder_2_out5);
  and and_7 (out_3[1], not_19_out, not_20_out);
  not not_20 (not_20_out, decoder_2_out6);
  not not_21 (out_3[2], decoder_2_out2);
  not not_22 (not_22_out, decoder_2_out1);
  not not_23 (not_23_out, decoder_2_out4);
  and and_8 (out_3[3], not_22_out, not_23_out, not_24_out, not_25_out);
  not not_24 (not_24_out, decoder_2_out9);
  not not_25 (not_25_out, decoder_2_out7);
  or or_2 (out_3[4], decoder_2_out2, decoder_2_out0, decoder_2_out6, decoder_2_out8);
  not not_26 (not_26_out, decoder_2_out1);
  not not_27 (not_27_out, decoder_2_out2);
  and and_9 (out_3[5], not_26_out, not_27_out, not_28_out, not_29_out);
  not not_28 (not_28_out, decoder_2_out7);
  not not_29 (not_29_out, decoder_2_out3);
  not not_30 (not_30_out, decoder_2_out0);
  and and_10 (out_3[6], not_30_out, not_31_out, not_32_out);
  not not_31 (not_31_out, decoder_2_out1);
  not not_32 (not_32_out, decoder_2_out7);
  Decoder #(.select(4), .enable("false")) decoder_3 (
    .out0(decoder_3_out0), .out1(decoder_3_out1), .out2(decoder_3_out2), .out3(decoder_3_out3),
    .out4(decoder_3_out4), .out5(decoder_3_out5), .out6(decoder_3_out6), .out7(decoder_3_out7),
    .out8(decoder_3_out8), .out9(decoder_3_out9), .out10(decoder_3_out10), .out11(decoder_3_out11),
    .out12(decoder_3_out12), .out13(decoder_3_out13), .out14(decoder_3_out14), .out15(decoder_3_out15),
    .sel({2'b00, disp_help_three_shift_6_out_8}));
  not not_33 (not_33_out, decoder_3_out1);
  and top_bar (out_2[0], not_33_out, not_34_out);
  not not_34 (not_34_out, decoder_3_out4);
  not not_35 (not_35_out, decoder_3_out5);
  and top_right (out_2[1], not_35_out, not_36_out);
  not not_36 (not_36_out, decoder_3_out6);
  not bottom_right (out_2[2], decoder_3_out2);
  not not_37 (not_37_out, decoder_3_out1);
  not not_38 (not_38_out, decoder_3_out4);
  and bottom_bar (out_2[3], not_37_out, not_38_out, not_39_out, not_40_out);
  not not_39 (not_39_out, decoder_3_out9);
  not not_40 (not_40_out, decoder_3_out7);
  or bottom_left (out_2[4], decoder_3_out2, decoder_3_out0, decoder_3_out6, decoder_3_out8);
  not not_41 (not_41_out, decoder_3_out1);
  not not_42 (not_42_out, decoder_3_out2);
  and top_left (out_2[5], not_41_out, not_42_out, not_43_out, not_44_out);
  not not_43 (not_43_out, decoder_3_out7);
  not not_44 (not_44_out, decoder_3_out3);
  not not_45 (not_45_out, decoder_3_out0);
  not not_46 (not_46_out, decoder_3_out1);
  and middle_bar (out_2[6], not_45_out, not_46_out, not_47_out);
  not not_47 (not_47_out, decoder_3_out7);
endmodule

module PROG_ROM (
  input  Tick_on,
  output Working,
  output RAM_M,
  output RAM_M_W,
  output [7:0] Instr_O,
  output [7:0] Addr_O,
  output A_W,
  output D_W
);

  wire and_2_out, and_5_out, and_6_out, and_7_out, and_8_out, and_9_out, and_10_out, and_11_out, and_12_out,
       and_13_out, and_14_out, and_15_out, and_16_out, and_17_out, and_18_out, and_19_out, and_20_out,
       and_21_out, clock_1_out, nand_1_out, not_1_out, not_2_out, not_3_out, not_4_out, not_5_out, not_6_out,
       not_7_out, not_8_out, not_9_out, not_10_out, not_11_out, not_12_out, not_13_out, not_14_out,
       not_15_out, not_16_out, not_17_out, not_18_out, not_19_out, not_20_out, not_21_out, not_22_out,
       not_23_out, not_24_out, not_25_out, not_26_out, not_27_out, not_28_out, not_29_out, not_30_out,
       not_31_out, not_32_out, not_33_out, not_34_out, not_35_out, not_36_out, or_1_out, or_2_out, or_3_out,
       or_4_out, or_5_out, or_6_out, or_7_out, or_8_out, or_9_out, or_10_out, or_11_out, or_12_out,
       or_13_out, or_14_out, or_15_out, or_16_out, or_17_out, or_18_out, or_19_out, or_20_out, or_21_out,
       or_22_out, or_23_out, or_24_out, or_25_out, or_26_out, or_27_out, or_28_out, or_29_out, or_30_out,
       or_31_out, or_32_out, or_33_out, or_34_out, or_35_out, or_36_out, or_37_out, or_38_out, or_39_out,
       or_40_out, or_41_out, or_42_out, or_43_out, or_44_out, or_45_out, or_46_out, or_50_out, or_51_out,
       or_52_out, or_53_out, or_54_out, or_55_out, or_56_out, or_57_out, or_58_out, or_59_out, or_60_out,
       or_61_out, or_62_out, or_63_out, or_64_out, or_65_out, or_66_out, or_67_out, or_68_out, or_69_out,
       or_70_out, or_71_out, or_72_out, or_73_out, or_74_out, or_75_out, or_76_out, or_77_out, or_78_out,
       or_79_out, or_82_out, or_83_out, or_84_out, or_85_out, or_86_out, or_87_out, or_88_out, or_89_out,
       or_90_out, or_91_out, or_92_out, or_93_out, or_94_out, or_95_out, or_96_out, or_97_out, or_98_out,
       or_99_out, or_100_out, or_101_out, or_102_out, or_103_out, or_104_out, or_105_out, or_106_out,
       or_107_out, or_108_out, or_109_out, or_110_out, or_111_out, or_112_out, or_113_out, or_114_out,
       or_115_out, or_116_out, or_117_out, or_118_out, or_119_out, or_120_out, or_121_out, or_122_out,
       or_123_out, or_124_out, or_125_out, or_126_out, t_ff_2_qn, t_ff_3_qn, t_ff_4_q, t_ff_4_qn, t_ff_5_q,
       t_ff_6_qn;
  wire [3:0] t_ff_2_q;
  wire [7:0] or_127_out;

  T_Flip_Flop t_ff_1 (.T(1'b1), .clk(or_1_out), .Q(Working));  // open: Qn, reset, preset
  or or_1 (or_1_out, Tick_on, and_21_out);
  T_Flip_Flop t_ff_2 (.T(1'b1), .clk(RAM_M_W), .Q(t_ff_2_q[0]), .Qn(t_ff_2_qn));  // open: reset, preset
  Clock clock_1 (.out(clock_1_out));
  not not_1 (not_1_out, t_ff_4_q);
  not not_2 (not_2_out, t_ff_5_q);
  and and_1 (A_W, not_1_out, Working, not_2_out);
  T_Flip_Flop t_ff_3 (.T(1'b1), .clk(t_ff_2_qn), .Q(t_ff_2_q[1]), .Qn(t_ff_3_qn));  // open: reset, preset
  T_Flip_Flop t_ff_4 (.T(1'b1), .clk(and_2_out), .Q(t_ff_4_q), .Qn(t_ff_4_qn), .reset(and_5_out));  // open: preset
  and and_2 (and_2_out, clock_1_out, Working);
  not not_3 (not_3_out, t_ff_5_q);
  not not_4 (not_4_out, t_ff_4_q);
  and and_3 (D_W, t_ff_4_q, Working, not_3_out);
  and and_4 (RAM_M_W, not_4_out, Working, t_ff_5_q);
  and and_5 (and_5_out, t_ff_4_q, Working, t_ff_5_q);
  T_Flip_Flop t_ff_5 (.T(1'b1), .clk(t_ff_4_qn), .Q(t_ff_5_q), .reset(and_5_out));  // open: Qn, preset
  T_Flip_Flop t_ff_6 (.T(1'b1), .clk(t_ff_3_qn), .Q(t_ff_2_q[2]), .Qn(t_ff_6_qn));  // open: reset, preset
  T_Flip_Flop t_ff_7 (.T(1'b1), .clk(t_ff_6_qn), .Q(t_ff_2_q[3]));  // open: Qn, reset, preset
  not not_5 (not_5_out, t_ff_2_q[3]);
  not not_6 (not_6_out, t_ff_2_q[2]);
  and and_6 (and_6_out, not_5_out, not_6_out, not_7_out, not_8_out);
  not not_7 (not_7_out, t_ff_2_q[1]);
  not not_8 (not_8_out, t_ff_2_q[0]);
  not not_9 (not_9_out, t_ff_2_q[3]);
  not not_10 (not_10_out, t_ff_2_q[2]);
  and and_7 (and_7_out, not_9_out, not_10_out, not_11_out, t_ff_2_q[0]);
  not not_11 (not_11_out, t_ff_2_q[1]);
  not not_12 (not_12_out, t_ff_2_q[3]);
  not not_13 (not_13_out, t_ff_2_q[2]);
  and and_8 (and_8_out, not_12_out, not_13_out, t_ff_2_q[1], not_14_out);
  not not_14 (not_14_out, t_ff_2_q[0]);
  not not_15 (not_15_out, t_ff_2_q[3]);
  not not_16 (not_16_out, t_ff_2_q[2]);
  and and_9 (and_9_out, not_15_out, not_16_out, t_ff_2_q[1], t_ff_2_q[0]);
  not not_17 (not_17_out, t_ff_2_q[3]);
  and and_10 (and_10_out, not_17_out, t_ff_2_q[2], not_18_out, not_19_out);
  not not_18 (not_18_out, t_ff_2_q[1]);
  not not_19 (not_19_out, t_ff_2_q[0]);
  not not_20 (not_20_out, t_ff_2_q[3]);
  and and_11 (and_11_out, not_20_out, t_ff_2_q[2], not_21_out, t_ff_2_q[0]);
  not not_21 (not_21_out, t_ff_2_q[1]);
  not not_22 (not_22_out, t_ff_2_q[3]);
  and and_12 (and_12_out, not_22_out, t_ff_2_q[2], t_ff_2_q[1], not_23_out);
  not not_23 (not_23_out, t_ff_2_q[0]);
  not not_24 (not_24_out, t_ff_2_q[3]);
  and and_13 (and_13_out, not_24_out, t_ff_2_q[2], t_ff_2_q[1], t_ff_2_q[0]);
  not not_25 (not_25_out, t_ff_2_q[2]);
  and and_14 (and_14_out, t_ff_2_q[3], not_25_out, not_26_out, not_27_out);
  not not_26 (not_26_out, t_ff_2_q[1]);
  not not_27 (not_27_out, t_ff_2_q[0]);
  not not_28 (not_28_out, t_ff_2_q[2]);
  and and_15 (and_15_out, t_ff_2_q[3], not_28_out, not_29_out, t_ff_2_q[0]);
  not not_29 (not_29_out, t_ff_2_q[1]);
  not not_30 (not_30_out, t_ff_2_q[2]);
  and and_16 (and_16_out, t_ff_2_q[3], not_30_out, t_ff_2_q[1], not_31_out);
  not not_31 (not_31_out, t_ff_2_q[0]);
  not not_32 (not_32_out, t_ff_2_q[2]);
  and and_17 (and_17_out, t_ff_2_q[3], not_32_out, t_ff_2_q[1], t_ff_2_q[0]);
  and and_18 (and_18_out, t_ff_2_q[3], t_ff_2_q[2], not_33_out, not_34_out);
  not not_33 (not_33_out, t_ff_2_q[1]);
  not not_34 (not_34_out, t_ff_2_q[0]);
  and and_19 (and_19_out, t_ff_2_q[3], t_ff_2_q[2], not_35_out, t_ff_2_q[0]);
  not not_35 (not_35_out, t_ff_2_q[1]);
  and and_20 (and_20_out, t_ff_2_q[3], t_ff_2_q[2], t_ff_2_q[1], not_36_out);
  not not_36 (not_36_out, t_ff_2_q[0]);
  and and_21 (and_21_out, t_ff_2_q[3], t_ff_2_q[2], t_ff_2_q[1], t_ff_2_q[0]);
  assign Addr_O = A_W ? {4'b0000, t_ff_2_q} : 8'bz;  // Controlled_Buffer controlled_buffer_1
  buf or_2 (or_2_out, 1'b0);  // OR_Gate
  or or_3 (or_3_out, and_6_out, 1'b0);
  buf or_4 (or_4_out, 1'b0);  // OR_Gate
  buf or_5 (or_5_out, or_4_out);  // OR_Gate
  buf or_6 (or_6_out, or_2_out);  // OR_Gate
  or or_7 (or_7_out, and_7_out, or_3_out);
  buf or_8 (or_8_out, or_5_out);  // OR_Gate
  or or_9 (or_9_out, and_8_out, or_6_out);
  or or_10 (or_10_out, and_8_out, or_7_out);
  buf or_11 (or_11_out, or_9_out);  // OR_Gate
  or or_12 (or_12_out, and_9_out, or_8_out);
  or or_13 (or_13_out, and_9_out, or_10_out);
  or or_14 (or_14_out, and_10_out, or_13_out);
  buf or_15 (or_15_out, or_11_out);  // OR_Gate
  buf or_16 (or_16_out, or_12_out);  // OR_Gate
  buf or_17 (or_17_out, or_15_out);  // OR_Gate
  or or_18 (or_18_out, and_11_out, or_14_out);
  buf or_19 (or_19_out, or_16_out);  // OR_Gate
  or or_20 (or_20_out, and_12_out, or_18_out);
  buf or_21 (or_21_out, or_19_out);  // OR_Gate
  or or_22 (or_22_out, and_12_out, or_17_out);
  buf or_23 (or_23_out, or_22_out);  // OR_Gate
  or or_24 (or_24_out, and_13_out, or_20_out);
  or or_25 (or_25_out, and_13_out, or_21_out);
  buf or_26 (or_26_out, or_25_out);  // OR_Gate
  or or_27 (or_27_out, and_14_out, or_23_out);
  or or_28 (or_28_out, and_14_out, or_24_out);
  buf or_29 (or_29_out, or_26_out);  // OR_Gate
  or or_30 (or_30_out, and_15_out, or_27_out);
  buf or_31 (or_31_out, or_28_out);  // OR_Gate
  or or_32 (or_32_out, and_16_out, or_31_out);
  buf or_33 (or_33_out, or_30_out);  // OR_Gate
  buf or_34 (or_34_out, or_29_out);  // OR_Gate
  or or_35 (or_35_out, and_17_out, or_33_out);
  buf or_36 (or_36_out, or_34_out);  // OR_Gate
  or or_37 (or_37_out, and_17_out, or_32_out);
  buf or_38 (or_38_out, or_36_out);  // OR_Gate
  buf or_39 (or_39_out, or_37_out);  // OR_Gate
  buf or_40 (or_40_out, or_35_out);  // OR_Gate
  buf or_41 (or_41_out, or_40_out);  // OR_Gate
  buf or_42 (or_42_out, or_39_out);  // OR_Gate
  buf or_43 (or_43_out, or_38_out);  // OR_Gate
  buf or_44 (or_44_out, or_42_out);  // OR_Gate
  buf or_45 (or_45_out, or_43_out);  // OR_Gate
  buf or_46 (or_46_out, or_41_out);  // OR_Gate
  buf or_47 (or_127_out[7], or_44_out);  // OR_Gate
  buf or_48 (or_127_out[6], or_46_out);  // OR_Gate
  buf or_49 (or_127_out[5], or_45_out);  // OR_Gate
  buf or_50 (or_50_out, 1'b0);  // OR_Gate
  or or_51 (or_51_out, and_6_out, 1'b0);
  or or_52 (or_52_out, and_7_out, or_50_out);
  or or_53 (or_53_out, and_7_out, or_51_out);
  buf or_54 (or_54_out, or_53_out);  // OR_Gate
  buf or_55 (or_55_out, or_52_out);  // OR_Gate
  or or_56 (or_56_out, and_9_out, or_54_out);
  or or_57 (or_57_out, and_9_out, or_55_out);
  or or_58 (or_58_out, and_10_out, or_56_out);
  buf or_59 (or_59_out, or_57_out);  // OR_Gate
  or or_60 (or_60_out, and_11_out, or_58_out);
  or or_61 (or_61_out, and_11_out, or_59_out);
  buf or_62 (or_62_out, or_61_out);  // OR_Gate
  buf or_63 (or_63_out, or_60_out);  // OR_Gate
  or or_64 (or_64_out, and_13_out, or_63_out);
  or or_65 (or_65_out, and_13_out, or_62_out);
  or or_66 (or_66_out, and_14_out, or_65_out);
  buf or_67 (or_67_out, or_64_out);  // OR_Gate
  buf or_68 (or_68_out, or_67_out);  // OR_Gate
  or or_69 (or_69_out, and_15_out, or_66_out);
  or or_70 (or_70_out, and_16_out, or_68_out);
  buf or_71 (or_71_out, or_69_out);  // OR_Gate
  buf or_72 (or_72_out, or_70_out);  // OR_Gate
  or or_73 (or_73_out, and_17_out, or_71_out);
  buf or_74 (or_74_out, or_73_out);  // OR_Gate
  buf or_75 (or_75_out, or_72_out);  // OR_Gate
  buf or_76 (or_76_out, or_75_out);  // OR_Gate
  buf or_77 (or_77_out, or_74_out);  // OR_Gate
  buf or_78 (or_78_out, or_76_out);  // OR_Gate
  buf or_79 (or_79_out, or_77_out);  // OR_Gate
  buf or_80 (or_127_out[3], or_78_out);  // OR_Gate
  buf or_81 (or_127_out[4], or_79_out);  // OR_Gate
  or or_82 (or_82_out, and_6_out, 1'b0);
  buf or_83 (or_83_out, 1'b0);  // OR_Gate
  or or_84 (or_84_out, and_6_out, 1'b0);
  or or_85 (or_85_out, and_7_out, or_83_out);
  or or_86 (or_86_out, and_7_out, or_82_out);
  or or_87 (or_87_out, and_7_out, or_84_out);
  buf or_88 (or_88_out, or_86_out);  // OR_Gate
  buf or_89 (or_89_out, or_85_out);  // OR_Gate
  or or_90 (or_90_out, and_8_out, or_87_out);
  or or_91 (or_91_out, and_9_out, or_88_out);
  or or_92 (or_92_out, and_9_out, or_89_out);
  or or_93 (or_93_out, and_9_out, or_90_out);
  or or_94 (or_94_out, and_10_out, or_93_out);
  buf or_95 (or_95_out, or_92_out);  // OR_Gate
  buf or_96 (or_96_out, or_91_out);  // OR_Gate
  or or_97 (or_97_out, and_11_out, or_95_out);
  buf or_98 (or_98_out, or_96_out);  // OR_Gate
  or or_99 (or_99_out, and_11_out, or_94_out);
  or or_100 (or_100_out, and_12_out, or_99_out);
  buf or_101 (or_101_out, or_98_out);  // OR_Gate
  buf or_102 (or_102_out, or_97_out);  // OR_Gate
  buf or_103 (or_103_out, or_101_out);  // OR_Gate
  or or_104 (or_104_out, and_13_out, or_100_out);
  or or_105 (or_105_out, and_13_out, or_102_out);
  buf or_106 (or_106_out, or_103_out);  // OR_Gate
  buf or_107 (or_107_out, or_105_out);  // OR_Gate
  or or_108 (or_108_out, and_14_out, or_104_out);
  buf or_109 (or_109_out, or_107_out);  // OR_Gate
  buf or_110 (or_110_out, or_108_out);  // OR_Gate
  buf or_111 (or_111_out, or_106_out);  // OR_Gate
  or or_112 (or_112_out, and_16_out, or_110_out);
  or or_113 (or_113_out, and_16_out, or_109_out);
  or or_114 (or_114_out, and_16_out, or_111_out);
  buf or_115 (or_115_out, or_112_out);  // OR_Gate
  buf or_116 (or_116_out, or_113_out);  // OR_Gate
  buf or_117 (or_117_out, or_114_out);  // OR_Gate
  buf or_118 (or_118_out, or_116_out);  // OR_Gate
  or or_119 (or_119_out, and_18_out, or_117_out);
  buf or_120 (or_120_out, or_115_out);  // OR_Gate
  or or_121 (or_121_out, and_19_out, or_118_out);
  or or_122 (or_122_out, and_19_out, or_120_out);
  or or_123 (or_123_out, and_19_out, or_119_out);
  buf or_124 (or_124_out, or_123_out);  // OR_Gate
  buf or_125 (or_125_out, or_121_out);  // OR_Gate
  buf or_126 (or_126_out, or_122_out);  // OR_Gate
  buf or_127 (or_127_out[0], or_124_out);  // OR_Gate
  buf or_128 (or_127_out[1], or_125_out);  // OR_Gate
  buf or_129 (or_127_out[2], or_126_out);  // OR_Gate
  assign Instr_O = D_W ? or_127_out : 8'bz;  // Controlled_Buffer controlled_buffer_2
  nand nand_1 (nand_1_out, and_21_out, RAM_M_W);
  and and_22 (RAM_M, nand_1_out, RAM_M_W);
endmodule

module PC (
  input  [7:0] I,
  input  W,
  input  in_3,
  output [7:0] O
);

  D_Flip_Flop #(.trigger("high")) d_ff_1 (.D(I[0]), .clk(W), .Q(O[0]), .reset(in_3));  // open: Qn, preset
  D_Flip_Flop #(.trigger("high")) d_ff_2 (.D(I[1]), .clk(W), .Q(O[1]), .reset(in_3));  // open: Qn, preset
  D_Flip_Flop #(.trigger("high")) d_ff_3 (.D(I[2]), .clk(W), .Q(O[2]), .reset(in_3));  // open: Qn, preset
  D_Flip_Flop #(.trigger("high")) d_ff_4 (.D(I[3]), .clk(W), .Q(O[3]), .reset(in_3));  // open: Qn, preset
  D_Flip_Flop #(.trigger("high")) d_ff_5 (.D(I[4]), .clk(W), .Q(O[4]), .reset(in_3));  // open: Qn, preset
  D_Flip_Flop #(.trigger("high")) d_ff_6 (.D(I[5]), .clk(W), .Q(O[5]), .reset(in_3));  // open: Qn, preset
  D_Flip_Flop #(.trigger("high")) d_ff_7 (.D(I[6]), .clk(W), .Q(O[6]), .reset(in_3));  // open: Qn, preset
  D_Flip_Flop #(.trigger("high")) d_ff_8 (.D(I[7]), .clk(W), .Q(O[7]), .reset(in_3));  // open: Qn, preset
endmodule

module selector_thing (
  input  in_1,
  input  [7:0] in_2,
  input  in_3,
  output out_4
);

  wire and_1_out, and_2_out, and_3_out, and_4_out, not_1_out, not_2_out, not_3_out, not_4_out, not_5_out,
       not_6_out;

  and and_1 (and_1_out, in_1, in_2[0], not_1_out);
  not not_1 (not_1_out, in_3);
  not not_2 (not_2_out, in_2[0]);
  and and_2 (and_2_out, in_1, not_2_out, in_3);
  not not_3 (not_3_out, and_1_out);
  not not_4 (not_4_out, and_2_out);
  not not_5 (not_5_out, not_3_out);
  and and_3 (and_3_out, not_5_out, and_1_out);
  not not_6 (not_6_out, not_4_out);
  and and_4 (and_4_out, not_6_out, and_2_out);
  or or_1 (out_4, and_3_out, and_4_out);
endmodule

module PROG_ROM_VER2 (
  input  RESET,
  input  Tick_on,
  output Working,
  output RAM_M,
  output RAM_M_W,
  output [7:0] Instr_O,
  output [7:0] Addr_O,
  output A_W,
  output D_W,
  output CPU_ON
);

  wire and_2_out, and_3_out, clock_1_out, N0000_out, N0001_out, N0010_out, N0011_out, N0100_out, N0101_out,
       N0110_out, N0111_out, N1000_out, N1001_out, N1010_out, N1011_out, N1100_out, N1101_out, N1110_out,
       N1111_out, nand_1_out, not_1_out, not_2_out, not_3_out, not_4_out, not_5_out, not_6_out, not_7_out,
       not_8_out, not_9_out, not_10_out, not_11_out, not_12_out, not_13_out, not_14_out, not_15_out,
       not_16_out, not_17_out, not_18_out, not_19_out, not_20_out, not_21_out, not_22_out, not_23_out,
       not_24_out, not_25_out, not_26_out, not_27_out, not_28_out, not_29_out, not_30_out, not_31_out,
       not_32_out, not_33_out, not_34_out, not_35_out, not_36_out, or_1_out, or_2_out, or_3_out, or_4_out,
       or_5_out, or_6_out, or_7_out, or_8_out, or_9_out, or_10_out, or_11_out, or_12_out, or_13_out,
       or_14_out, or_15_out, or_16_out, or_17_out, or_18_out, or_19_out, or_20_out, or_21_out, or_22_out,
       or_23_out, or_24_out, or_25_out, or_26_out, or_27_out, or_28_out, or_29_out, or_30_out, or_31_out,
       or_32_out, or_33_out, or_34_out, or_35_out, or_36_out, or_37_out, or_38_out, or_39_out, or_40_out,
       or_41_out, or_42_out, or_43_out, or_44_out, or_45_out, or_46_out, or_47_out, or_51_out, or_52_out,
       or_53_out, or_54_out, or_55_out, or_56_out, or_57_out, or_58_out, or_59_out, or_60_out, or_61_out,
       or_62_out, or_63_out, or_64_out, or_65_out, or_66_out, or_67_out, or_68_out, or_69_out, or_70_out,
       or_71_out, or_72_out, or_73_out, or_74_out, or_75_out, or_76_out, or_77_out, or_78_out, or_79_out,
       or_80_out, or_83_out, or_84_out, or_85_out, or_86_out, or_87_out, or_88_out, or_89_out, or_90_out,
       or_91_out, or_92_out, or_93_out, or_94_out, or_95_out, or_96_out, or_97_out, or_98_out, or_99_out,
       or_100_out, or_101_out, or_102_out, or_103_out, or_104_out, or_105_out, or_106_out, or_107_out,
       or_108_out, or_109_out, or_110_out, or_111_out, or_112_out, or_113_out, or_114_out, or_115_out,
       or_116_out, or_117_out, or_118_out, or_119_out, or_120_out, or_121_out, or_122_out, or_123_out,
       or_124_out, or_125_out, or_126_out, or_127_out, t_ff_1_qn, t_ff_3_qn, t_ff_4_qn, t_ff_5_q, t_ff_5_qn,
       t_ff_6_q, t_ff_7_qn;
  wire [3:0] t_ff_3_q;
  wire [7:0] or_130_out;

  T_Flip_Flop t_ff_1 (.T(1'b1), .clk(or_1_out), .Q(Working), .Qn(t_ff_1_qn));  // open: reset, preset
  or or_1 (or_1_out, Tick_on, N1111_out);
  T_Flip_Flop t_ff_2 (.T(1'b1), .clk(t_ff_1_qn), .Q(CPU_ON), .reset(RESET));  // open: Qn, preset
  T_Flip_Flop t_ff_3 (.T(1'b1), .clk(RAM_M_W), .Q(t_ff_3_q[0]), .Qn(t_ff_3_qn), .reset(RESET));  // open: preset
  Clock clock_1 (.out(clock_1_out));
  not not_1 (not_1_out, t_ff_6_q);
  not not_2 (not_2_out, t_ff_5_q);
  and and_1 (A_W, not_2_out, Working, not_1_out);
  T_Flip_Flop t_ff_4 (.T(1'b1), .clk(t_ff_3_qn), .Q(t_ff_3_q[1]), .Qn(t_ff_4_qn), .reset(RESET));  // open: preset
  T_Flip_Flop t_ff_5 (.T(1'b1), .clk(and_2_out), .Q(t_ff_5_q), .Qn(t_ff_5_qn), .reset(or_2_out));  // open: preset
  and and_2 (and_2_out, clock_1_out, Working);
  not not_3 (not_3_out, t_ff_6_q);
  not not_4 (not_4_out, t_ff_5_q);
  and and_3 (and_3_out, t_ff_5_q, Working, t_ff_6_q);
  and and_4 (RAM_M_W, not_4_out, Working, t_ff_6_q);
  and and_5 (D_W, t_ff_5_q, Working, not_3_out);
  T_Flip_Flop t_ff_6 (.T(1'b1), .clk(t_ff_5_qn), .Q(t_ff_6_q), .reset(or_2_out));  // open: Qn, preset
  T_Flip_Flop t_ff_7 (.T(1'b1), .clk(t_ff_4_qn), .Q(t_ff_3_q[2]), .Qn(t_ff_7_qn), .reset(RESET));  // open: preset
  or or_2 (or_2_out, RESET, and_3_out);
  T_Flip_Flop t_ff_8 (.T(1'b1), .clk(t_ff_7_qn), .Q(t_ff_3_q[3]), .reset(RESET));  // open: Qn, preset
  not not_5 (not_5_out, t_ff_3_q[3]);
  not not_6 (not_6_out, t_ff_3_q[2]);
  and N0000 (N0000_out, not_5_out, not_6_out, not_7_out, not_8_out);
  not not_7 (not_7_out, t_ff_3_q[1]);
  not not_8 (not_8_out, t_ff_3_q[0]);
  not not_9 (not_9_out, t_ff_3_q[3]);
  not not_10 (not_10_out, t_ff_3_q[2]);
  and N0001 (N0001_out, not_9_out, not_10_out, not_11_out, t_ff_3_q[0]);
  not not_11 (not_11_out, t_ff_3_q[1]);
  not not_12 (not_12_out, t_ff_3_q[3]);
  not not_13 (not_13_out, t_ff_3_q[2]);
  and N0010 (N0010_out, not_12_out, not_13_out, t_ff_3_q[1], not_14_out);
  not not_14 (not_14_out, t_ff_3_q[0]);
  not not_15 (not_15_out, t_ff_3_q[3]);
  not not_16 (not_16_out, t_ff_3_q[2]);
  and N0011 (N0011_out, not_15_out, not_16_out, t_ff_3_q[1], t_ff_3_q[0]);
  not not_17 (not_17_out, t_ff_3_q[3]);
  and N0100 (N0100_out, not_17_out, t_ff_3_q[2], not_18_out, not_19_out);
  not not_18 (not_18_out, t_ff_3_q[1]);
  not not_19 (not_19_out, t_ff_3_q[0]);
  not not_20 (not_20_out, t_ff_3_q[3]);
  and N0101 (N0101_out, not_20_out, t_ff_3_q[2], not_21_out, t_ff_3_q[0]);
  not not_21 (not_21_out, t_ff_3_q[1]);
  not not_22 (not_22_out, t_ff_3_q[3]);
  and N0110 (N0110_out, not_22_out, t_ff_3_q[2], t_ff_3_q[1], not_23_out);
  not not_23 (not_23_out, t_ff_3_q[0]);
  not not_24 (not_24_out, t_ff_3_q[3]);
  and N0111 (N0111_out, not_24_out, t_ff_3_q[2], t_ff_3_q[1], t_ff_3_q[0]);
  not not_25 (not_25_out, t_ff_3_q[2]);
  and N1000 (N1000_out, t_ff_3_q[3], not_25_out, not_26_out, not_27_out);
  not not_26 (not_26_out, t_ff_3_q[1]);
  not not_27 (not_27_out, t_ff_3_q[0]);
  not not_28 (not_28_out, t_ff_3_q[2]);
  and N1001 (N1001_out, t_ff_3_q[3], not_28_out, not_29_out, t_ff_3_q[0]);
  not not_29 (not_29_out, t_ff_3_q[1]);
  not not_30 (not_30_out, t_ff_3_q[2]);
  and N1010 (N1010_out, t_ff_3_q[3], not_30_out, t_ff_3_q[1], not_31_out);
  not not_31 (not_31_out, t_ff_3_q[0]);
  not not_32 (not_32_out, t_ff_3_q[2]);
  and N1011 (N1011_out, t_ff_3_q[3], not_32_out, t_ff_3_q[1], t_ff_3_q[0]);
  and N1100 (N1100_out, t_ff_3_q[3], t_ff_3_q[2], not_33_out, not_34_out);
  not not_33 (not_33_out, t_ff_3_q[1]);
  not not_34 (not_34_out, t_ff_3_q[0]);
  and N1101 (N1101_out, t_ff_3_q[3], t_ff_3_q[2], not_35_out, t_ff_3_q[0]);
  not not_35 (not_35_out, t_ff_3_q[1]);
  and N1110 (N1110_out, t_ff_3_q[3], t_ff_3_q[2], t_ff_3_q[1], not_36_out);
  not not_36 (not_36_out, t_ff_3_q[0]);
  and N1111 (N1111_out, t_ff_3_q[3], t_ff_3_q[2], t_ff_3_q[1], t_ff_3_q[0]);
  assign Addr_O = A_W ? {4'b0000, t_ff_3_q} : 8'bz;  // Controlled_Buffer controlled_buffer_1
  buf or_3 (or_3_out, 1'b0);  // OR_Gate
  or or_4 (or_4_out, N0000_out, 1'b0);
  or or_5 (or_5_out, N0000_out, 1'b0);
  buf or_6 (or_6_out, or_4_out);  // OR_Gate
  or or_7 (or_7_out, N0001_out, or_5_out);
  buf or_8 (or_8_out, or_3_out);  // OR_Gate
  or or_9 (or_9_out, N0010_out, or_6_out);
  buf or_10 (or_10_out, or_8_out);  // OR_Gate
  or or_11 (or_11_out, N0010_out, or_7_out);
  buf or_12 (or_12_out, or_9_out);  // OR_Gate
  or or_13 (or_13_out, N0011_out, or_11_out);
  or or_14 (or_14_out, N0011_out, or_10_out);
  buf or_15 (or_15_out, or_12_out);  // OR_Gate
  or or_16 (or_16_out, N0100_out, or_13_out);
  buf or_17 (or_17_out, or_14_out);  // OR_Gate
  or or_18 (or_18_out, N0101_out, or_16_out);
  buf or_19 (or_19_out, or_15_out);  // OR_Gate
  buf or_20 (or_20_out, or_17_out);  // OR_Gate
  buf or_21 (or_21_out, or_20_out);  // OR_Gate
  or or_22 (or_22_out, N0110_out, or_18_out);
  or or_23 (or_23_out, N0110_out, or_19_out);
  buf or_24 (or_24_out, or_23_out);  // OR_Gate
  or or_25 (or_25_out, N0111_out, or_22_out);
  or or_26 (or_26_out, N0111_out, or_21_out);
  buf or_27 (or_27_out, or_24_out);  // OR_Gate
  buf or_28 (or_28_out, or_26_out);  // OR_Gate
  or or_29 (or_29_out, N1000_out, or_25_out);
  buf or_30 (or_30_out, or_29_out);  // OR_Gate
  buf or_31 (or_31_out, or_28_out);  // OR_Gate
  or or_32 (or_32_out, N1001_out, or_27_out);
  buf or_33 (or_33_out, or_32_out);  // OR_Gate
  or or_34 (or_34_out, N1010_out, or_30_out);
  buf or_35 (or_35_out, or_31_out);  // OR_Gate
  or or_36 (or_36_out, N1011_out, or_34_out);
  buf or_37 (or_37_out, or_35_out);  // OR_Gate
  or or_38 (or_38_out, N1011_out, or_33_out);
  buf or_39 (or_39_out, or_36_out);  // OR_Gate
  buf or_40 (or_40_out, or_38_out);  // OR_Gate
  buf or_41 (or_41_out, or_37_out);  // OR_Gate
  buf or_42 (or_42_out, or_40_out);  // OR_Gate
  buf or_43 (or_43_out, or_41_out);  // OR_Gate
  buf or_44 (or_44_out, or_39_out);  // OR_Gate
  buf or_45 (or_45_out, or_42_out);  // OR_Gate
  buf or_46 (or_46_out, or_44_out);  // OR_Gate
  buf or_47 (or_47_out, or_43_out);  // OR_Gate
  buf or_48 (or_130_out[7], or_46_out);  // OR_Gate
  buf or_49 (or_130_out[6], or_45_out);  // OR_Gate
  buf or_50 (or_130_out[5], or_47_out);  // OR_Gate
  or or_51 (or_51_out, N0000_out, 1'b0);
  buf or_52 (or_52_out, 1'b0);  // OR_Gate
  or or_53 (or_53_out, N0001_out, or_51_out);
  or or_54 (or_54_out, N0001_out, or_52_out);
  buf or_55 (or_55_out, or_53_out);  // OR_Gate
  buf or_56 (or_56_out, or_54_out);  // OR_Gate
  or or_57 (or_57_out, N0011_out, or_56_out);
  or or_58 (or_58_out, N0011_out, or_55_out);
  or or_59 (or_59_out, N0100_out, or_58_out);
  or or_60 (or_60_out, N0100_out, or_57_out);
  buf or_61 (or_61_out, or_59_out);  // OR_Gate
  or or_62 (or_62_out, N0101_out, or_60_out);
  or or_63 (or_63_out, N0110_out, or_62_out);
  buf or_64 (or_64_out, or_61_out);  // OR_Gate
  buf or_65 (or_65_out, or_64_out);  // OR_Gate
  or or_66 (or_66_out, N0111_out, or_63_out);
  or or_67 (or_67_out, N1000_out, or_66_out);
  or or_68 (or_68_out, N1000_out, or_65_out);
  or or_69 (or_69_out, N1001_out, or_68_out);
  buf or_70 (or_70_out, or_67_out);  // OR_Gate
  or or_71 (or_71_out, N1010_out, or_70_out);
  buf or_72 (or_72_out, or_69_out);  // OR_Gate
  buf or_73 (or_73_out, or_71_out);  // OR_Gate
  or or_74 (or_74_out, N1011_out, or_72_out);
  buf or_75 (or_75_out, or_74_out);  // OR_Gate
  buf or_76 (or_76_out, or_73_out);  // OR_Gate
  buf or_77 (or_77_out, or_75_out);  // OR_Gate
  buf or_78 (or_78_out, or_76_out);  // OR_Gate
  buf or_79 (or_79_out, or_78_out);  // OR_Gate
  buf or_80 (or_80_out, or_77_out);  // OR_Gate
  buf or_81 (or_130_out[4], or_80_out);  // OR_Gate
  buf or_82 (or_130_out[3], or_79_out);  // OR_Gate
  or or_83 (or_83_out, N0000_out, 1'b0);
  buf or_84 (or_84_out, 1'b0);  // OR_Gate
  buf or_85 (or_85_out, 1'b0);  // OR_Gate
  or or_86 (or_86_out, N0001_out, or_85_out);
  or or_87 (or_87_out, N0001_out, or_83_out);
  or or_88 (or_88_out, N0001_out, or_84_out);
  or or_89 (or_89_out, N0010_out, or_87_out);
  buf or_90 (or_90_out, or_88_out);  // OR_Gate
  buf or_91 (or_91_out, or_86_out);  // OR_Gate
  or or_92 (or_92_out, N0011_out, or_90_out);
  or or_93 (or_93_out, N0011_out, or_89_out);
  or or_94 (or_94_out, N0011_out, or_91_out);
  buf or_95 (or_95_out, or_94_out);  // OR_Gate
  or or_96 (or_96_out, N0100_out, or_92_out);
  or or_97 (or_97_out, N0100_out, or_93_out);
  buf or_98 (or_98_out, or_95_out);  // OR_Gate
  buf or_99 (or_99_out, or_96_out);  // OR_Gate
  or or_100 (or_100_out, N0101_out, or_97_out);
  buf or_101 (or_101_out, or_100_out);  // OR_Gate
  or or_102 (or_102_out, N0110_out, or_98_out);
  buf or_103 (or_103_out, or_99_out);  // OR_Gate
  or or_104 (or_104_out, N0111_out, or_103_out);
  buf or_105 (or_105_out, or_102_out);  // OR_Gate
  or or_106 (or_106_out, N0111_out, or_101_out);
  or or_107 (or_107_out, N1000_out, or_105_out);
  or or_108 (or_108_out, N1000_out, or_106_out);
  buf or_109 (or_109_out, or_104_out);  // OR_Gate
  buf or_110 (or_110_out, or_108_out);  // OR_Gate
  buf or_111 (or_111_out, or_109_out);  // OR_Gate
  buf or_112 (or_112_out, or_107_out);  // OR_Gate
  or or_113 (or_113_out, N1010_out, or_110_out);
  or or_114 (or_114_out, N1010_out, or_111_out);
  or or_115 (or_115_out, N1010_out, or_112_out);
  buf or_116 (or_116_out, or_115_out);  // OR_Gate
  buf or_117 (or_117_out, or_114_out);  // OR_Gate
  buf or_118 (or_118_out, or_113_out);  // OR_Gate
  buf or_119 (or_119_out, or_118_out);  // OR_Gate
  or or_120 (or_120_out, N1100_out, or_117_out);
  buf or_121 (or_121_out, or_116_out);  // OR_Gate
  or or_122 (or_122_out, N1101_out, or_119_out);
  or or_123 (or_123_out, N1101_out, or_121_out);
  or or_124 (or_124_out, N1101_out, or_120_out);
  buf or_125 (or_125_out, or_122_out);  // OR_Gate
  buf or_126 (or_126_out, or_123_out);  // OR_Gate
  buf or_127 (or_127_out, or_124_out);  // OR_Gate
  buf or_128 (or_130_out[1], or_126_out);  // OR_Gate
  buf or_129 (or_130_out[2], or_125_out);  // OR_Gate
  buf or_130 (or_130_out[0], or_127_out);  // OR_Gate
  assign Instr_O = D_W ? or_130_out : 8'bz;  // Controlled_Buffer controlled_buffer_2
  nand nand_1 (nand_1_out, N1111_out, RAM_M_W);
  and and_6 (RAM_M, nand_1_out, RAM_M_W);
endmodule

module test_reset_button (
  input  in_1,
  input  [5:0] in_2,
  output [5:0] out_3
);

  wire and_1_out, button_1_out, not_1_out, not_2_out;

  Button button_1 (.out(button_1_out));
  not not_1 (not_1_out, in_1);
  not not_2 (not_2_out, not_1_out);
  and and_1 (and_1_out, in_1, not_2_out);
  D_Flip_Flop #(.trigger("high")) d_ff_1 (
    .D(in_2[0]), .clk(and_1_out), .Q(out_3[5]), .reset(button_1_out));  // open: Qn, preset
  D_Flip_Flop #(.trigger("high")) d_ff_2 (
    .D(in_2[1]), .clk(and_1_out), .Q(out_3[4]), .reset(button_1_out));  // open: Qn, preset
  D_Flip_Flop #(.trigger("high")) d_ff_3 (
    .D(in_2[2]), .clk(and_1_out), .Q(out_3[3]), .reset(button_1_out));  // open: Qn, preset
  D_Flip_Flop #(.trigger("high")) d_ff_4 (
    .D(in_2[3]), .clk(and_1_out), .Q(out_3[2]), .reset(button_1_out));  // open: Qn, preset
  D_Flip_Flop #(.trigger("high")) d_ff_5 (
    .D(in_2[4]), .clk(and_1_out), .Q(out_3[1]), .reset(button_1_out));  // open: Qn, preset
  D_Flip_Flop #(.trigger("high")) d_ff_6 (
    .D(in_2[5]), .clk(and_1_out), .Q(out_3[0]), .reset(button_1_out));  // open: Qn, preset
endmodule
