// Logisim project CU.circ as structural Verilog
module OP_ROM (
  input  [7:0] IRin,
  input  ACTV,
  output ADD,
  output SUB,
  output MULT,
  output LD,
  output SAV,
  output BEQ,
  output BNQ,
  output PRT,
  output INP,
  output STOP,
  output FLSH
);

  wire and_1_out, and_3_out, and_5_out, and_7_out, and_9_out, and_11_out, and_13_out, and_15_out, and_17_out,
       and_19_out, and_21_out, not_1_out, not_2_out, not_3_out, not_4_out, not_5_out, not_6_out, not_7_out,
       not_8_out, not_9_out, not_10_out, not_11_out, not_12_out, not_13_out, not_14_out, not_15_out,
       not_16_out, not_17_out, not_18_out, not_19_out, not_20_out, not_21_out, not_22_out, not_23_out,
       not_24_out, not_25_out, not_26_out, not_27_out, not_28_out, not_29_out, not_30_out, not_31_out,
       or_1_out;

  not not_1 (not_1_out, IRin[3]);
  not not_2 (not_2_out, IRin[4]);
  not not_3 (not_3_out, IRin[5]);
  not not_4 (not_4_out, IRin[4]);
  not not_5 (not_5_out, IRin[5]);
  not not_6 (not_6_out, IRin[5]);
  not not_7 (not_7_out, IRin[6]);
  not not_8 (not_8_out, IRin[6]);
  or or_1 (or_1_out, IRin[4], IRin[5]);
  not not_9 (not_9_out, IRin[6]);
  not not_10 (not_10_out, IRin[7]);
  not not_11 (not_11_out, IRin[7]);
  not not_12 (not_12_out, IRin[2]);
  not not_13 (not_13_out, IRin[3]);
  not not_14 (not_14_out, IRin[5]);
  not not_15 (not_15_out, IRin[3]);
  not not_16 (not_16_out, IRin[5]);
  not not_17 (not_17_out, IRin[1]);
  not not_18 (not_18_out, IRin[2]);
  not not_19 (not_19_out, IRin[3]);
  not not_20 (not_20_out, IRin[4]);
  not not_21 (not_21_out, IRin[5]);
  not not_22 (not_22_out, IRin[6]);
  not not_23 (not_23_out, IRin[7]);
  not not_24 (not_24_out, IRin[0]);
  not not_25 (not_25_out, IRin[1]);
  not not_26 (not_26_out, IRin[2]);
  not not_27 (not_27_out, IRin[3]);
  not not_28 (not_28_out, IRin[4]);
  not not_29 (not_29_out, IRin[5]);
  not not_30 (not_30_out, IRin[6]);
  not not_31 (not_31_out, IRin[7]);
  and and_1 (and_1_out, not_1_out, not_2_out, not_3_out, IRin[6], IRin[7]);
  and and_2 (ADD, and_1_out, ACTV);
  and and_3 (and_3_out, IRin[3], not_4_out, not_5_out, IRin[6], IRin[7]);
  and and_4 (SUB, and_3_out, ACTV);
  and and_5 (and_5_out, IRin[5], IRin[6], IRin[7]);
  and and_6 (MULT, and_5_out, ACTV);
  and and_7 (and_7_out, not_6_out, not_7_out, IRin[7]);
  and and_8 (LD, and_7_out, ACTV);
  and and_9 (and_9_out, IRin[5], not_8_out, IRin[7]);
  and and_10 (SAV, and_9_out, ACTV);
  and and_11 (and_11_out, or_1_out, not_9_out, not_10_out);
  and and_12 (BEQ, and_11_out, ACTV);
  and and_13 (and_13_out, IRin[6], not_11_out);
  and and_14 (BNQ, and_13_out, ACTV);
  and and_15 (and_15_out, not_12_out, not_13_out, IRin[4], not_14_out, IRin[6], IRin[7]);
  and and_16 (PRT, and_15_out, ACTV);
  and and_17 (and_17_out, IRin[2], not_15_out, IRin[4], not_16_out, IRin[6], IRin[7]);
  and and_18 (INP, and_17_out, ACTV);
  and and_19 (and_19_out, IRin[0], not_17_out, not_18_out, not_19_out, not_20_out, not_21_out, not_22_out, not_23_out);
  and and_20 (STOP, and_19_out, ACTV);
  and and_21 (and_21_out, not_24_out, not_25_out, not_26_out, not_27_out, not_28_out, not_29_out, not_30_out, not_31_out);
  and and_22 (FLSH, and_21_out, ACTV);
endmodule

module CU (
  input  [7:0] IRin,
  input  RESET_AFTER_RUN,
  input  Initial_On_Keep_On,
  output Instructing,
  output Fetching,
  output Reg0,
  output Reg1,
  output R_W,
  output ALU_L,
  output ALU_R,
  output ALU_O,
  output ALU_EXE,
  output ALU_FLAG,
  output STAT,
  output MAR_IN,
  output MAR_OUT,
  output MBR_IN,
  output MBR_OUT,
  output IR,
  output PC_INC,
  output PC_A_I,
  output [7:0] PC_A_O,
  output PC_OUT,
  output BRANCH_SIGN,
  output DR_OUT,
  output DR_IN,
  output AR_IN,
  output RAM_R,
  output RAM_W,
  output [7:0] RAM_A,
  output PNT,
  output INPT
);

  wire add_sub_1_alu_exe, add_sub_1_alu_l, add_sub_1_alu_o, add_sub_1_alu_r, add_sub_1_done, add_sub_1_r0,
       add_sub_1_r1, add_sub_1_r_w, bnq_beq_1_alu_l, bnq_beq_1_alu_r, bnq_beq_1_alue_exe, bnq_beq_1_done,
       bnq_beq_1_pc_a_i, bnq_beq_1_r0, bnq_beq_1_r1, bnq_beq_1_sgn, bnq_beq_1_stat, fetch_1_ar, fetch_1_done,
       fetch_1_dr_o, fetch_1_ir, fetch_1_mar_i, fetch_1_mar_o, fetch_1_mbr_i, fetch_1_mbr_o, fetch_1_pc_inc,
       fetch_1_pc_o, fetch_1_ram_r, inp_1_done, inp_1_inpt, inp_1_mbr_i, inp_1_mbr_o, inp_1_r0_i, inp_1_r1_i,
       ld_1_ar_i, ld_1_done, ld_1_dr_o, ld_1_mar_i, ld_1_mar_o, ld_1_mbr_i, ld_1_mbr_o, ld_1_r0_i, ld_1_r1_i,
       ld_1_ram_r, op_rom_1_add, op_rom_1_beq, op_rom_1_bnq, op_rom_1_inp, op_rom_1_ld, op_rom_1_prt,
       op_rom_1_sav, op_rom_1_sub, or_1_out, or_2_out, or_3_out, or_4_out, or_7_out, or_8_out, or_9_out,
       or_10_out, or_11_out, or_12_out, or_13_out, or_14_out, or_15_out, or_16_out, or_17_out, or_18_out,
       or_19_out, or_20_out, or_21_out, or_22_out, or_24_out, or_25_out, or_26_out, or_27_out, or_28_out,
       or_29_out, or_30_out, or_31_out, or_32_out, or_33_out, or_34_out, or_35_out, or_36_out, or_37_out,
       or_38_out, or_39_out, or_40_out, or_41_out, or_42_out, or_43_out, prt_1_disp, prt_1_done, prt_1_mbr_i,
       prt_1_mbr_o, prt_1_r0_o, prt_1_r1_o, sav_1_ar_in, sav_1_done, sav_1_dr_in, sav_1_mar_in,
       sav_1_mar_out, sav_1_mbr_in, sav_1_mbr_out, sav_1_r0_out, sav_1_r1_out, sav_1_ram_w, t_ff_1_q,
       t_ff_1_qn;
  wire [3:0] bnq_beq_1_pc_a_o, ld_1_ram_a, or_23_out, sav_1_ram_a;
  wire [3:3] clock_1_out;

  Clock clock_1 (.out(clock_1_out[3]));
  OP_ROM op_rom_1 (
    .IRin(IRin), .LD(op_rom_1_ld), .BEQ(op_rom_1_beq), .ADD(op_rom_1_add), .SAV(op_rom_1_sav),
    .SUB(op_rom_1_sub), .PRT(op_rom_1_prt), .INP(op_rom_1_inp), .BNQ(op_rom_1_bnq), .ACTV(t_ff_1_q));  // open: STOP, MULT, FLSH
  assign PC_A_O[3:0] = bnq_beq_1_pc_a_o & {4{clock_1_out[3]}};  // AND_Gate and_1, 4 bits wide
  assign RAM_A[3:0] = or_23_out & {4{clock_1_out[3]}};  // AND_Gate and_2, 4 bits wide
  or or_1 (or_1_out, op_rom_1_add, op_rom_1_sub);
  ADD_SUB add_sub_1 (
    .ALU_O(add_sub_1_alu_o), .ALU_EXE(add_sub_1_alu_exe), .ALU_R(add_sub_1_alu_r), .ALU_L(add_sub_1_alu_l),
    .R1(add_sub_1_r1), .R0(add_sub_1_r0), .Actv(or_1_out), .IRin(IRin), .R_W(add_sub_1_r_w),
    .DONE(add_sub_1_done));
  or or_2 (or_2_out, add_sub_1_done, or_11_out);
  or or_3 (or_3_out, add_sub_1_r_w, or_12_out);
  and and_3 (R_W, clock_1_out[3], or_3_out);
  and and_4 (ALU_L, clock_1_out[3], or_7_out);
  and and_5 (ALU_R, clock_1_out[3], or_8_out);
  and and_6 (ALU_O, clock_1_out[3], add_sub_1_alu_o);
  and and_7 (ALU_EXE, clock_1_out[3], or_9_out);
  and and_8 (ALU_FLAG, clock_1_out[3], op_rom_1_sub);
  and and_9 (STAT, clock_1_out[3], bnq_beq_1_stat);
  and and_10 (MAR_IN, clock_1_out[3], or_21_out);
  and and_11 (MAR_OUT, clock_1_out[3], or_22_out);
  and and_12 (MBR_IN, clock_1_out[3], or_16_out);
  and and_13 (MBR_OUT, clock_1_out[3], or_17_out);
  and and_14 (IR, clock_1_out[3], fetch_1_ir);
  and and_15 (PC_INC, clock_1_out[3], fetch_1_pc_inc);
  and and_16 (PC_A_I, clock_1_out[3], bnq_beq_1_pc_a_i);
  and and_17 (PC_OUT, clock_1_out[3], fetch_1_pc_o);
  and and_18 (BRANCH_SIGN, clock_1_out[3], bnq_beq_1_sgn);
  and and_19 (DR_OUT, clock_1_out[3], or_18_out);
  and and_20 (DR_IN, clock_1_out[3], sav_1_dr_in);
  and and_21 (AR_IN, clock_1_out[3], or_19_out);
  and and_22 (RAM_R, clock_1_out[3], or_20_out);
  and and_23 (RAM_W, clock_1_out[3], sav_1_ram_w);
  and and_24 (PNT, clock_1_out[3], prt_1_disp);
  and and_25 (INPT, clock_1_out[3], inp_1_inpt);
  or or_4 (or_4_out, RESET_AFTER_RUN, or_2_out);
  or or_5 (Reg0, add_sub_1_r0, or_13_out);
  or or_6 (Reg1, add_sub_1_r1, or_14_out);
  or or_7 (or_7_out, add_sub_1_alu_l, bnq_beq_1_alu_l);
  or or_8 (or_8_out, add_sub_1_alu_r, bnq_beq_1_alu_r);
  or or_9 (or_9_out, add_sub_1_alu_exe, bnq_beq_1_alue_exe);
  T_Flip_Flop t_ff_1 (.T(1'b1), .clk(or_4_out), .Q(t_ff_1_q), .Qn(t_ff_1_qn));  // open: reset, preset
  or or_10 (or_10_out, op_rom_1_beq, op_rom_1_bnq);
  or or_11 (or_11_out, ld_1_done, or_24_out);
  or or_12 (or_12_out, ld_1_r1_i, or_15_out);
  LD ld_1 (
    .AR_I(ld_1_ar_i), .R0_I(ld_1_r0_i), .MBR_I(ld_1_mbr_i), .DONE(ld_1_done), .MBR_O(ld_1_mbr_o),
    .RAM_A(ld_1_ram_a), .ACTV(op_rom_1_ld), .MAR_I(ld_1_mar_i), .MAR_O(ld_1_mar_o), .IR_I(IRin),
    .DR_O(ld_1_dr_o), .R1_I(ld_1_r1_i), .RAM_R(ld_1_ram_r));
  or or_13 (or_13_out, ld_1_r0_i, or_26_out);
  or or_14 (or_14_out, ld_1_r1_i, or_27_out);
  or or_15 (or_15_out, ld_1_r0_i, or_41_out);
  or or_16 (or_16_out, ld_1_mbr_i, or_30_out);
  or or_17 (or_17_out, ld_1_mbr_o, or_25_out);
  or or_18 (or_18_out, ld_1_dr_o, fetch_1_dr_o);
  or or_19 (or_19_out, ld_1_ar_i, or_31_out);
  or or_20 (or_20_out, ld_1_ram_r, fetch_1_ram_r);
  and and_26 (Fetching, t_ff_1_qn, Initial_On_Keep_On);
  or or_21 (or_21_out, ld_1_mar_i, or_28_out);
  or or_22 (or_22_out, ld_1_mar_o, or_29_out);
  assign or_23_out = ld_1_ram_a | sav_1_ram_a;  // OR_Gate or_23, 4 bits wide
  SAV sav_1 (
    .R0_OUT(sav_1_r0_out), .R1_OUT(sav_1_r1_out), .MBR_IN(sav_1_mbr_in), .IR_IN(IRin), .MAR_IN(sav_1_mar_in),
    .DONE(sav_1_done), .AR_IN(sav_1_ar_in), .ACTV(op_rom_1_sav), .MAR_OUT(sav_1_mar_out),
    .RAM_W(sav_1_ram_w), .RAM_A(sav_1_ram_a), .DR_IN(sav_1_dr_in), .MBR_OUT(sav_1_mbr_out));
  or or_24 (or_24_out, sav_1_done, or_32_out);
  or or_25 (or_25_out, sav_1_mbr_out, or_36_out);
  not not_1 (Instructing, Fetching);
  or or_26 (or_26_out, sav_1_r0_out, or_33_out);
  or or_27 (or_27_out, sav_1_r1_out, or_34_out);
  or or_28 (or_28_out, sav_1_mar_in, fetch_1_mar_i);
  or or_29 (or_29_out, sav_1_mar_out, fetch_1_mar_o);
  or or_30 (or_30_out, sav_1_mbr_in, or_39_out);
  or or_31 (or_31_out, sav_1_ar_in, fetch_1_ar);
  BNQ_BEQ bnq_beq_1 (
    .DONE(bnq_beq_1_done), .Actv(or_10_out), .ALU_L(bnq_beq_1_alu_l), .ALUE_EXE(bnq_beq_1_alue_exe),
    .STAT(bnq_beq_1_stat), .R1(bnq_beq_1_r1), .IRin(IRin), .PC_A_I(bnq_beq_1_pc_a_i),
    .ALU_R(bnq_beq_1_alu_r), .R0(bnq_beq_1_r0), .PC_A_O(bnq_beq_1_pc_a_o), .SGN(bnq_beq_1_sgn));
  or or_32 (or_32_out, bnq_beq_1_done, or_35_out);
  or or_33 (or_33_out, bnq_beq_1_r0, or_37_out);
  or or_34 (or_34_out, bnq_beq_1_r1, or_38_out);
  PRT prt_1 (
    .DISP(prt_1_disp), .R0_O(prt_1_r0_o), .IR_I(IRin), .MBR_I(prt_1_mbr_i), .MBR_O(prt_1_mbr_o),
    .R1_O(prt_1_r1_o), .ACTV(op_rom_1_prt), .DONE(prt_1_done));
  or or_35 (or_35_out, prt_1_done, or_40_out);
  or or_36 (or_36_out, prt_1_mbr_o, or_42_out);
  or or_37 (or_37_out, prt_1_r0_o, inp_1_r0_i);
  or or_38 (or_38_out, prt_1_r1_o, inp_1_r1_i);
  or or_39 (or_39_out, prt_1_mbr_i, or_43_out);
  FETCH fetch_1 (
    .MBR_O(fetch_1_mbr_o), .IR(fetch_1_ir), .MAR_O(fetch_1_mar_o), .MBR_I(fetch_1_mbr_i), .ACTV(Fetching),
    .PC_O(fetch_1_pc_o), .DR_O(fetch_1_dr_o), .MAR_I(fetch_1_mar_i), .AR(fetch_1_ar),
    .PC_INC(fetch_1_pc_inc), .DONE(fetch_1_done), .RAM_R(fetch_1_ram_r));
  INP inp_1 (
    .MBR_I(inp_1_mbr_i), .R1_I(inp_1_r1_i), .INPT(inp_1_inpt), .R0_I(inp_1_r0_i), .MBR_O(inp_1_mbr_o),
    .IR_I(IRin), .ACTV(op_rom_1_inp), .DONE(inp_1_done));
  or or_40 (or_40_out, inp_1_done, fetch_1_done);
  or or_41 (or_41_out, inp_1_r1_i, inp_1_r0_i);
  or or_42 (or_42_out, inp_1_mbr_o, fetch_1_mbr_o);
  or or_43 (or_43_out, inp_1_mbr_i, fetch_1_mbr_i);

  assign PC_A_O[7:4] = 4'b0000;
  assign RAM_A[7:4] = 4'b0000;

  // Notes on the sheet:
  //   Control Gates
endmodule

module ADD_SUB (
  input  [7:0] IRin,
  input  Actv,
  output R0,
  output R1,
  output ALU_L,
  output ALU_R,
  output ALU_EXE,
  output ALU_O,
  output R_W,
  output DONE
);

  wire and_1_out, and_2_out, clock_1_out, demultiplexer_1_out0, demultiplexer_1_out1, EXE_out, LOAD1_out,
       LOAD2_out, not_1_out, not_2_out, not_3_out, not_4_out, not_5_out, not_6_out, not_7_out, not_8_out,
       not_9_out, not_10_out, not_11_out, not_12_out, not_13_out, not_14_out, not_15_out, not_16_out,
       not_17_out, not_18_out, not_19_out, not_20_out, not_21_out, not_22_out, not_23_out, not_24_out,
       not_25_out, not_26_out, not_27_out, not_28_out, or_1_out, or_2_out, or_3_out, or_4_out, or_5_out,
       RESET_out, SAVE_out, t_ff_1_q, t_ff_1_qn, t_ff_2_q, t_ff_2_qn, t_ff_3_q;

  T_Flip_Flop t_ff_1 (
    .T(or_1_out), .clk(clock_1_out), .Q(t_ff_1_q), .Qn(t_ff_1_qn), .reset(not_1_out));  // open: preset
  or or_1 (or_1_out, Actv, SAVE_out);
  Clock clock_1 (.out(clock_1_out));
  not not_1 (not_1_out, not_2_out);
  not not_2 (not_2_out, not_8_out);
  not not_3 (not_3_out, clock_1_out);
  not not_4 (not_4_out, not_3_out);
  not not_5 (not_5_out, not_4_out);
  not not_6 (not_6_out, not_5_out);
  not not_7 (not_7_out, not_6_out);
  not not_8 (not_8_out, not_12_out);
  not not_9 (not_9_out, not_7_out);
  not not_10 (not_10_out, not_9_out);
  not not_11 (not_11_out, not_10_out);
  or or_2 (or_2_out, not_11_out, SAVE_out);
  T_Flip_Flop t_ff_2 (.T(or_1_out), .clk(t_ff_1_qn), .Q(t_ff_2_q), .Qn(t_ff_2_qn), .reset(not_8_out));  // open: preset
  not not_12 (not_12_out, RESET_out);
  not not_13 (not_13_out, not_14_out);
  not not_14 (not_14_out, not_15_out);
  not not_15 (not_15_out, or_2_out);
  T_Flip_Flop t_ff_3 (.T(or_1_out), .clk(t_ff_2_qn), .Q(t_ff_3_q), .reset(not_8_out));  // open: Qn, preset
  not not_16 (not_16_out, not_18_out);
  not not_17 (not_17_out, not_13_out);
  not not_18 (not_18_out, not_17_out);
  not not_19 (not_19_out, not_16_out);
  not not_20 (not_20_out, not_19_out);
  not not_21 (not_21_out, t_ff_2_q);
  and LOAD1 (LOAD1_out, t_ff_1_q, not_21_out, not_20_out, not_22_out);
  not not_22 (not_22_out, t_ff_3_q);
  not not_23 (not_23_out, t_ff_1_q);
  and LOAD2 (LOAD2_out, not_23_out, t_ff_2_q, not_20_out, not_24_out);
  not not_24 (not_24_out, t_ff_3_q);
  and EXE (EXE_out, t_ff_1_q, t_ff_2_q, not_20_out, not_25_out);
  not not_25 (not_25_out, t_ff_3_q);
  not not_26 (not_26_out, t_ff_1_q);
  not not_27 (not_27_out, t_ff_2_q);
  and SAVE (SAVE_out, not_26_out, not_27_out, not_20_out, t_ff_3_q);
  not not_28 (not_28_out, t_ff_2_q);
  and RESET (RESET_out, t_ff_1_q, not_28_out, not_20_out, t_ff_3_q);
  or or_3 (or_3_out, SAVE_out, LOAD1_out);
  and and_1 (and_1_out, IRin[1], LOAD2_out);
  and and_2 (and_2_out, IRin[2], or_3_out);
  or or_4 (or_4_out, and_2_out, and_1_out);
  or or_5 (or_5_out, or_3_out, LOAD2_out);
  Demultiplexer #(.enable("false")) demultiplexer_1 (
    .out0(demultiplexer_1_out0), .out1(demultiplexer_1_out1), .in(or_5_out), .sel(or_4_out));
  and and_3 (R0, Actv, demultiplexer_1_out0);
  and and_4 (R1, Actv, demultiplexer_1_out1);
  and and_5 (ALU_L, Actv, LOAD1_out);
  and and_6 (ALU_R, Actv, LOAD2_out);
  and and_7 (ALU_EXE, Actv, EXE_out);
  and and_8 (ALU_O, Actv, SAVE_out);
  and and_9 (R_W, Actv, SAVE_out);
  and and_10 (DONE, Actv, RESET_out);
endmodule

module BNQ_BEQ (
  input  [7:0] IRin,
  input  Actv,
  output [3:0] PC_A_O,
  output R0,
  output R1,
  output ALU_L,
  output ALU_R,
  output ALUE_EXE,
  output STAT,
  output PC_A_I,
  output DONE,
  output SGN
);

  wire and_1_out, and_2_out, clock_1_out, not_1_out, not_2_out, not_3_out, not_4_out, not_5_out, not_6_out,
       not_7_out, not_8_out, not_9_out, not_10_out, not_11_out, not_12_out, not_13_out, not_14_out,
       not_15_out, not_16_out, not_17_out, not_18_out, not_19_out, not_20_out, not_21_out, not_22_out,
       not_23_out, not_24_out, or_1_out, or_2_out, or_3_out, or_4_out, RESET_out, t_ff_1_q, t_ff_1_qn,
       t_ff_2_q, t_ff_2_qn, t_ff_3_q;

  T_Flip_Flop t_ff_1 (
    .T(or_1_out), .clk(clock_1_out), .Q(t_ff_1_q), .Qn(t_ff_1_qn), .reset(RESET_out));  // open: preset
  or or_1 (or_1_out, Actv, DONE);
  Clock clock_1 (.out(clock_1_out));
  not not_1 (not_1_out, clock_1_out);
  not not_2 (not_2_out, not_1_out);
  not not_3 (not_3_out, not_2_out);
  not not_4 (not_4_out, not_3_out);
  not not_5 (not_5_out, not_4_out);
  not not_6 (not_6_out, not_5_out);
  not not_7 (not_7_out, not_6_out);
  not not_8 (not_8_out, not_7_out);
  or or_2 (or_2_out, not_8_out, DONE);
  T_Flip_Flop t_ff_2 (.T(or_1_out), .clk(t_ff_1_qn), .Q(t_ff_2_q), .Qn(t_ff_2_qn), .reset(RESET_out));  // open: preset
  not not_9 (not_9_out, not_10_out);
  not not_10 (not_10_out, or_2_out);
  not not_11 (not_11_out, not_9_out);
  T_Flip_Flop t_ff_3 (.T(or_1_out), .clk(t_ff_2_qn), .Q(t_ff_3_q), .reset(RESET_out));  // open: Qn, preset
  not not_12 (not_12_out, not_11_out);
  not not_13 (not_13_out, not_12_out);
  not not_14 (not_14_out, not_16_out);
  not not_15 (not_15_out, not_14_out);
  not not_16 (not_16_out, not_13_out);
  not not_17 (not_17_out, t_ff_2_q);
  and LOAD1 (ALU_L, t_ff_1_q, not_17_out, not_15_out, not_18_out);
  not not_18 (not_18_out, t_ff_3_q);
  not not_19 (not_19_out, t_ff_1_q);
  and LOAD2 (ALU_R, not_19_out, t_ff_2_q, not_15_out, not_20_out);
  not not_20 (not_20_out, t_ff_3_q);
  and EXE1 (ALUE_EXE, t_ff_1_q, t_ff_2_q, not_15_out, not_21_out);
  not not_21 (not_21_out, t_ff_3_q);
  not not_22 (not_22_out, t_ff_1_q);
  not not_23 (not_23_out, t_ff_2_q);
  and EXE2 (DONE, not_22_out, not_23_out, not_15_out, t_ff_3_q);
  not not_24 (not_24_out, t_ff_2_q);
  and RESET (RESET_out, t_ff_1_q, not_24_out, not_15_out, t_ff_3_q);
  and and_1 (and_1_out, IRin[4], ALU_R);
  and and_2 (and_2_out, IRin[5], ALU_L);
  and and_3 (PC_A_O[0], IRin[0], DONE);
  and and_4 (PC_A_O[1], IRin[1], DONE);
  and and_5 (PC_A_O[2], IRin[2], DONE);
  and and_6 (PC_A_O[3], IRin[3], DONE);
  or or_3 (or_3_out, and_2_out, and_1_out);
  Demultiplexer #(.enable("false")) demultiplexer_1 (.out0(R0), .out1(R1), .in(or_4_out), .sel(or_3_out));
  or or_4 (or_4_out, ALU_L, ALU_R);
  and and_7 (SGN, DONE, IRin[6]);

  assign PC_A_I = DONE;
  assign STAT = DONE;
endmodule

module FETCH (
  input  ACTV,
  output MAR_I,
  output PC_O,
  output MAR_O,
  output AR,
  output RAM_R,
  output MBR_I,
  output DR_O,
  output MBR_O,
  output IR,
  output PC_INC,
  output DONE
);

  wire and_3_out, and_7_out, clock_1_out, not_1_out, not_2_out, not_3_out, not_4_out, not_5_out, not_6_out,
       not_7_out, not_8_out, not_9_out, not_10_out, not_11_out, not_12_out, not_13_out, not_14_out,
       not_15_out, not_16_out, not_17_out, not_18_out, not_19_out, not_20_out, not_21_out, not_22_out,
       not_23_out, not_24_out, not_25_out, or_1_out, or_2_out, t_ff_1_q, t_ff_1_qn, t_ff_2_q, t_ff_2_qn,
       t_ff_3_q;

  T_Flip_Flop t_ff_1 (
    .T(or_1_out), .clk(clock_1_out), .Q(t_ff_1_q), .Qn(t_ff_1_qn), .reset(and_7_out));  // open: preset
  or or_1 (or_1_out, ACTV, DONE);
  Clock clock_1 (.out(clock_1_out));
  not not_1 (not_1_out, clock_1_out);
  not not_2 (not_2_out, not_1_out);
  not not_3 (not_3_out, not_2_out);
  not not_4 (not_4_out, not_3_out);
  not not_5 (not_5_out, not_4_out);
  not not_6 (not_6_out, not_5_out);
  not not_7 (not_7_out, not_6_out);
  not not_8 (not_8_out, not_7_out);
  or or_2 (or_2_out, not_8_out, DONE);
  T_Flip_Flop t_ff_2 (.T(or_1_out), .clk(t_ff_1_qn), .Q(t_ff_2_q), .Qn(t_ff_2_qn), .reset(and_7_out));  // open: preset
  not not_9 (not_9_out, not_10_out);
  not not_10 (not_10_out, or_2_out);
  T_Flip_Flop t_ff_3 (.T(or_1_out), .clk(t_ff_2_qn), .Q(t_ff_3_q), .reset(and_7_out));  // open: Qn, preset
  not not_11 (not_11_out, not_13_out);
  not not_12 (not_12_out, not_11_out);
  not not_13 (not_13_out, not_9_out);
  not not_14 (not_14_out, not_12_out);
  not not_15 (not_15_out, not_14_out);
  and and_1 (MAR_I, t_ff_1_q, not_25_out, not_16_out, not_17_out);
  not not_16 (not_16_out, t_ff_2_q);
  not not_17 (not_17_out, t_ff_3_q);
  not not_18 (not_18_out, t_ff_1_q);
  and and_2 (AR, not_18_out, not_25_out, t_ff_2_q, not_19_out);
  not not_19 (not_19_out, t_ff_3_q);
  and and_3 (and_3_out, t_ff_1_q, not_25_out, t_ff_2_q, not_20_out);
  not not_20 (not_20_out, t_ff_3_q);
  not not_21 (not_21_out, t_ff_1_q);
  and and_4 (DR_O, not_21_out, not_25_out, not_22_out, t_ff_3_q);
  not not_22 (not_22_out, t_ff_2_q);
  and and_5 (IR, t_ff_1_q, not_25_out, not_23_out, t_ff_3_q);
  not not_23 (not_23_out, t_ff_2_q);
  not not_24 (not_24_out, t_ff_1_q);
  and and_6 (DONE, not_24_out, t_ff_2_q, not_25_out, t_ff_3_q);
  and and_7 (and_7_out, t_ff_1_q, t_ff_2_q, not_25_out, t_ff_3_q);
  not not_25 (not_25_out, not_15_out);
  or or_3 (RAM_R, MAR_I, and_3_out);

  assign MAR_O = AR;
  assign MBR_I = DR_O;
  assign MBR_O = IR;
  assign PC_INC = DONE;
  assign PC_O = MAR_I;
endmodule

module SAV (
  input  [7:0] IR_IN,
  input  ACTV,
  output [3:0] RAM_A,
  output MAR_IN,
  output AR_IN,
  output MAR_OUT,
  output MBR_IN,
  output R0_OUT,
  output R1_OUT,
  output MBR_OUT,
  output DR_IN,
  output RAM_W,
  output DONE
);

  wire and_5_out, and_6_out, clock_1_out, not_1_out, not_2_out, not_3_out, not_4_out, not_5_out, not_6_out,
       not_7_out, not_8_out, not_9_out, not_10_out, not_11_out, not_12_out, not_13_out, not_14_out,
       not_15_out, not_16_out, not_17_out, not_18_out, not_19_out, not_20_out, not_21_out, not_22_out,
       not_23_out, not_24_out, or_1_out, or_2_out, t_ff_1_q, t_ff_1_qn, t_ff_2_q, t_ff_2_qn, t_ff_3_q,
       undriven, undriven_2, undriven_3, undriven_4;

  T_Flip_Flop t_ff_1 (
    .T(or_1_out), .clk(clock_1_out), .Q(t_ff_1_q), .Qn(t_ff_1_qn), .reset(and_6_out));  // open: preset
  or or_1 (or_1_out, ACTV, and_5_out);
  Clock clock_1 (.out(clock_1_out));
  not not_1 (not_1_out, clock_1_out);
  not not_2 (not_2_out, not_1_out);
  not not_3 (not_3_out, not_2_out);
  not not_4 (not_4_out, not_3_out);
  not not_5 (not_5_out, not_4_out);
  not not_6 (not_6_out, not_5_out);
  not not_7 (not_7_out, not_6_out);
  not not_8 (not_8_out, not_7_out);
  or or_2 (or_2_out, not_8_out, and_5_out);
  T_Flip_Flop t_ff_2 (.T(or_1_out), .clk(t_ff_1_qn), .Q(t_ff_2_q), .Qn(t_ff_2_qn), .reset(and_6_out));  // open: preset
  not not_9 (not_9_out, or_2_out);
  not not_10 (not_10_out, not_9_out);
  T_Flip_Flop t_ff_3 (.T(or_1_out), .clk(t_ff_2_qn), .Q(t_ff_3_q), .reset(and_6_out));  // open: Qn, preset
  not not_11 (not_11_out, not_13_out);
  not not_12 (not_12_out, not_10_out);
  not not_13 (not_13_out, not_12_out);
  not not_14 (not_14_out, not_15_out);
  not not_15 (not_15_out, not_11_out);
  not not_16 (not_16_out, not_14_out);
  not not_17 (not_17_out, t_ff_2_q);
  and and_1 (MAR_IN, t_ff_1_q, not_17_out, not_16_out, not_18_out);
  not not_18 (not_18_out, t_ff_3_q);
  not not_19 (not_19_out, t_ff_1_q);
  and and_2 (AR_IN, not_19_out, t_ff_2_q, not_16_out, not_20_out);
  not not_20 (not_20_out, t_ff_3_q);
  and and_3 (MBR_IN, t_ff_1_q, t_ff_2_q, not_16_out, not_21_out);
  not not_21 (not_21_out, t_ff_3_q);
  not not_22 (not_22_out, t_ff_1_q);
  not not_23 (not_23_out, t_ff_2_q);
  and and_4 (DR_IN, not_22_out, not_23_out, not_16_out, t_ff_3_q);
  not not_24 (not_24_out, t_ff_2_q);
  and and_5 (and_5_out, t_ff_1_q, not_24_out, not_16_out, t_ff_3_q);
  and and_6 (and_6_out, t_ff_1_q, t_ff_2_q, not_16_out, t_ff_3_q);
  and and_7 (RAM_W, ACTV, and_5_out);
  and and_8 (DONE, and_5_out, ACTV);
  and and_9 (RAM_A[0], IR_IN[0], MAR_IN);
  and and_10 (RAM_A[1], IR_IN[1], MAR_IN);
  and and_11 (RAM_A[2], IR_IN[2], MAR_IN);
  and and_12 (RAM_A[3], IR_IN[3], MAR_IN);
  Demultiplexer #(.enable("false")) demultiplexer_1 (.out0(R0_OUT), .out1(R1_OUT), .in(MBR_IN), .sel(IR_IN[4]));
  T_Flip_Flop t_ff_4 (.T(1'b1), .clk(MAR_IN), .reset(undriven));  // open: Q, Qn, preset
  T_Flip_Flop t_ff_5 (.T(1'b1), .clk(AR_IN), .reset(undriven_2), .preset(undriven));  // open: Q, Qn
  T_Flip_Flop t_ff_6 (.T(1'b1), .clk(MBR_IN), .reset(undriven_3), .preset(undriven_2));  // open: Q, Qn
  T_Flip_Flop t_ff_7 (.T(1'b1), .clk(DR_IN), .reset(undriven_4), .preset(undriven_3));  // open: Q, Qn
  T_Flip_Flop t_ff_8 (.T(1'b1), .clk(and_5_out), .preset(undriven_4));  // open: Q, Qn, reset

  assign MAR_OUT = AR_IN;
  assign MBR_OUT = DR_IN;
endmodule

module LD (
  input  [7:0] IR_I,
  input  ACTV,
  output [3:0] RAM_A,
  output MAR_I,
  output MAR_O,
  output AR_I,
  output RAM_R,
  output DR_O,
  output MBR_I,
  output MBR_O,
  output R0_I,
  output R1_I,
  output DONE
);

  wire and_3_out, and_6_out, clock_1_out, not_1_out, not_2_out, not_3_out, not_4_out, not_5_out, not_6_out,
       not_7_out, not_8_out, not_9_out, not_10_out, not_11_out, not_12_out, not_13_out, not_14_out,
       not_15_out, not_16_out, not_17_out, not_18_out, not_19_out, not_20_out, not_21_out, not_22_out,
       not_23_out, not_24_out, not_25_out, or_1_out, or_2_out, t_ff_1_q, t_ff_1_qn, t_ff_2_q, t_ff_2_qn,
       t_ff_3_q;

  T_Flip_Flop t_ff_1 (
    .T(or_1_out), .clk(clock_1_out), .Q(t_ff_1_q), .Qn(t_ff_1_qn), .reset(and_6_out));  // open: preset
  or or_1 (or_1_out, ACTV, DONE);
  Clock clock_1 (.out(clock_1_out));
  not not_1 (not_1_out, clock_1_out);
  not not_2 (not_2_out, not_1_out);
  not not_3 (not_3_out, not_2_out);
  not not_4 (not_4_out, not_3_out);
  not not_5 (not_5_out, not_4_out);
  not not_6 (not_6_out, not_5_out);
  not not_7 (not_7_out, not_6_out);
  not not_8 (not_8_out, not_7_out);
  or or_2 (or_2_out, not_8_out, DONE);
  not not_9 (not_9_out, or_2_out);
  T_Flip_Flop t_ff_2 (.T(or_1_out), .clk(t_ff_1_qn), .Q(t_ff_2_q), .Qn(t_ff_2_qn), .reset(and_6_out));  // open: preset
  not not_10 (not_10_out, not_11_out);
  not not_11 (not_11_out, not_9_out);
  T_Flip_Flop t_ff_3 (.T(or_1_out), .clk(t_ff_2_qn), .Q(t_ff_3_q), .reset(and_6_out));  // open: Qn, preset
  not not_12 (not_12_out, not_10_out);
  not not_13 (not_13_out, not_14_out);
  not not_14 (not_14_out, not_12_out);
  not not_15 (not_15_out, not_16_out);
  not not_16 (not_16_out, not_13_out);
  not not_17 (not_17_out, t_ff_2_q);
  and and_1 (MAR_I, t_ff_1_q, not_17_out, not_15_out, not_18_out);
  not not_18 (not_18_out, t_ff_3_q);
  not not_19 (not_19_out, t_ff_1_q);
  and and_2 (AR_I, not_19_out, t_ff_2_q, not_15_out, not_20_out);
  not not_20 (not_20_out, t_ff_3_q);
  and and_3 (and_3_out, t_ff_1_q, t_ff_2_q, not_15_out, not_21_out);
  not not_21 (not_21_out, t_ff_3_q);
  not not_22 (not_22_out, t_ff_1_q);
  not not_23 (not_23_out, t_ff_2_q);
  and and_4 (DR_O, not_22_out, not_23_out, not_15_out, t_ff_3_q);
  not not_24 (not_24_out, t_ff_2_q);
  and and_5 (DONE, t_ff_1_q, not_24_out, not_15_out, t_ff_3_q);
  not not_25 (not_25_out, t_ff_1_q);
  and and_6 (and_6_out, not_25_out, t_ff_2_q, not_15_out, t_ff_3_q);
  or or_3 (RAM_R, AR_I, and_3_out);
  and and_7 (RAM_A[0], IR_I[0], MAR_I);
  and and_8 (RAM_A[1], IR_I[1], MAR_I);
  and and_9 (RAM_A[2], IR_I[2], MAR_I);
  and and_10 (RAM_A[3], IR_I[3], MAR_I);
  Demultiplexer #(.enable("false")) demultiplexer_1 (.out0(R0_I), .out1(R1_I), .in(DONE), .sel(IR_I[4]));

  assign MAR_O = AR_I;
  assign MBR_I = DR_O;
  assign MBR_O = DONE;
endmodule

module PRT (
  input  [7:0] IR_I,
  input  ACTV,
  output MBR_I,
  output R0_O,
  output R1_O,
  output MBR_O,
  output DISP,
  output DONE
);

  wire and_3_out, clock_1_out, not_1_out, not_2_out, not_3_out, not_4_out, not_5_out, not_6_out, not_7_out,
       not_8_out, not_9_out, not_10_out, not_11_out, not_12_out, not_13_out, not_14_out, not_15_out,
       not_16_out, not_17_out, not_18_out, not_19_out, not_20_out, not_21_out, or_1_out, or_2_out, t_ff_1_q,
       t_ff_1_qn, t_ff_2_q, t_ff_2_qn, t_ff_3_q;

  T_Flip_Flop t_ff_1 (
    .T(or_1_out), .clk(clock_1_out), .Q(t_ff_1_q), .Qn(t_ff_1_qn), .reset(and_3_out));  // open: preset
  or or_1 (or_1_out, ACTV, DISP);
  Clock clock_1 (.out(clock_1_out));
  not not_1 (not_1_out, clock_1_out);
  not not_2 (not_2_out, not_1_out);
  not not_3 (not_3_out, not_2_out);
  not not_4 (not_4_out, not_3_out);
  not not_5 (not_5_out, not_4_out);
  not not_6 (not_6_out, not_5_out);
  not not_7 (not_7_out, not_6_out);
  not not_8 (not_8_out, not_7_out);
  or or_2 (or_2_out, not_8_out, DISP);
  not not_9 (not_9_out, or_2_out);
  T_Flip_Flop t_ff_2 (.T(or_1_out), .clk(t_ff_1_qn), .Q(t_ff_2_q), .Qn(t_ff_2_qn), .reset(and_3_out));  // open: preset
  not not_10 (not_10_out, not_9_out);
  not not_11 (not_11_out, not_10_out);
  T_Flip_Flop t_ff_3 (.T(or_1_out), .clk(t_ff_2_qn), .Q(t_ff_3_q), .reset(and_3_out));  // open: Qn, preset
  not not_12 (not_12_out, not_13_out);
  not not_13 (not_13_out, not_11_out);
  not not_14 (not_14_out, not_12_out);
  not not_15 (not_15_out, not_14_out);
  not not_16 (not_16_out, not_15_out);
  not not_17 (not_17_out, t_ff_2_q);
  and and_1 (MBR_I, t_ff_1_q, not_17_out, not_16_out, not_18_out);
  not not_18 (not_18_out, t_ff_3_q);
  not not_19 (not_19_out, t_ff_1_q);
  and and_2 (DISP, not_19_out, t_ff_2_q, not_16_out, not_20_out);
  not not_20 (not_20_out, t_ff_3_q);
  and and_3 (and_3_out, t_ff_1_q, t_ff_2_q, not_16_out, not_21_out);
  not not_21 (not_21_out, t_ff_3_q);
  Demultiplexer #(.enable("false")) demultiplexer_1 (.out0(R0_O), .out1(R1_O), .in(MBR_I), .sel(IR_I[1]));

  assign DONE = DISP;
  assign MBR_O = DISP;
endmodule

module INP (
  input  [7:0] IR_I,
  input  ACTV,
  output INPT,
  output MBR_I,
  output MBR_O,
  output DONE,
  output R0_I,
  output R1_I
);

  wire and_1_out, and_2_out, and_3_out, clock_1_out, demultiplexer_1_out0, demultiplexer_1_out1, not_1_out,
       not_2_out, not_3_out, not_4_out, not_5_out, not_6_out, not_7_out, not_8_out, not_9_out, not_10_out,
       not_11_out, not_12_out, not_13_out, not_14_out, not_15_out, not_16_out, not_17_out, not_18_out,
       or_1_out, or_2_out, t_ff_1_q, t_ff_1_qn, t_ff_2_q;

  T_Flip_Flop t_ff_1 (
    .T(or_1_out), .clk(clock_1_out), .Q(t_ff_1_q), .Qn(t_ff_1_qn), .reset(and_3_out));  // open: preset
  or or_1 (or_1_out, ACTV, and_2_out);
  Clock clock_1 (.out(clock_1_out));
  not not_1 (not_1_out, clock_1_out);
  not not_2 (not_2_out, not_1_out);
  not not_3 (not_3_out, not_2_out);
  not not_4 (not_4_out, not_3_out);
  not not_5 (not_5_out, not_4_out);
  not not_6 (not_6_out, not_5_out);
  not not_7 (not_7_out, not_6_out);
  not not_8 (not_8_out, not_7_out);
  or or_2 (or_2_out, not_8_out, and_2_out);
  not not_9 (not_9_out, or_2_out);
  T_Flip_Flop t_ff_2 (.T(or_1_out), .clk(t_ff_1_qn), .Q(t_ff_2_q), .reset(and_3_out));  // open: Qn, preset
  not not_10 (not_10_out, not_9_out);
  not not_11 (not_11_out, not_10_out);
  not not_12 (not_12_out, not_14_out);
  not not_13 (not_13_out, not_11_out);
  not not_14 (not_14_out, not_13_out);
  not not_15 (not_15_out, not_16_out);
  not not_16 (not_16_out, not_12_out);
  and and_1 (and_1_out, t_ff_1_q, not_15_out, not_17_out);
  not not_17 (not_17_out, t_ff_2_q);
  not not_18 (not_18_out, t_ff_1_q);
  and and_2 (and_2_out, not_18_out, not_15_out, t_ff_2_q);
  and and_3 (and_3_out, t_ff_1_q, not_15_out, t_ff_2_q);
  and and_4 (INPT, and_1_out, ACTV);
  and and_5 (MBR_I, and_1_out, ACTV);
  and and_6 (MBR_O, and_2_out, ACTV);
  and and_7 (DONE, and_2_out, ACTV);
  Demultiplexer #(.enable("false")) demultiplexer_1 (
    .out0(demultiplexer_1_out0), .out1(demultiplexer_1_out1), .in(and_2_out), .sel(IR_I[1]));
  and and_8 (R0_I, ACTV, demultiplexer_1_out0);
  and and_9 (R1_I, demultiplexer_1_out1, ACTV);
endmodule
