// Logisim project Four_Bits_Add_Sub.circ as structural Verilog: 6 circuits, main circuit Add_Sub_4Bits
module Add_Sub_4Bits (
  input  [3:0] A,
  input  [3:0] B,
  input  Add_Sub,
  output [3:0] R,
  output Zero,
  output Overflow
);

  wire not_1_out;
  wire [3:0] BitFlipper_bout;

  // Probe on A
  // Probe on B
  TwoSComplementConvert BitFlipper (.Bout(BitFlipper_bout), .Bin(B), .Flip(not_1_out));
  not not_1 (not_1_out, Add_Sub);
  Adder_4_bits adder_4_bits_1 (.Sum(R), .B(BitFlipper_bout), .A(A), .Overflow(Overflow), .Cin(not_1_out));
  // Probe on R
  IsZero iszero_1 (.ZeroOut(Zero), .Ain(R));

  // Notes on the sheet:
  //   Rigel Zifkin 260683139
  //   MAKE SURE THAT YOU OPENED THIS PROJECT IN "LOGISIM-EVOLUTION"
  //   YOU CAN FIND "LOGISIM-EVOLUTION" PRORAM IN THE ASSIGNMENT'S FOLDER
  //   DO NOT USE "LOGISIM" VERSION TO SOLVE THIS ASSIGNMENT!
endmodule

module Add_1Bit (
  input  A,
  input  B,
  input  Cin,
  output Sum,
  output Cout
);

  wire and_1_out, and_2_out, and_3_out, not_1_out, not_2_out, or_1_out, or_2_out;

  or or_1 (or_1_out, A, B);
  and and_1 (and_1_out, B, A);
  not not_1 (not_1_out, and_1_out);
  and and_2 (and_2_out, or_1_out, not_1_out);
  and and_3 (and_3_out, and_2_out, Cin);
  or or_2 (or_2_out, Cin, and_2_out);
  not not_2 (not_2_out, and_3_out);
  and and_4 (Sum, not_2_out, or_2_out);
  or or_3 (Cout, and_3_out, and_1_out);

  // Notes on the sheet:
  //   Rigel Zifkin 260683139
  //   MAKE SURE THAT YOU OPENED THIS PROJECT IN "LOGISIM-EVOLUTION"
  //   YOU CAN FIND "LOGISIM-EVOLUTION" PRORAM IN THE ASSIGNMENT'S FOLDER
  //   DO NOT USE "LOGISIM" VERSION TO SOLVE THIS ASSIGNMENT!
endmodule

module Adder_4_bits (
  input  Cin,
  input  [3:0] A,
  input  [3:0] B,
  output [3:0] Sum,
  output Overflow
);

  wire add_1bit_1_cout, add_1bit_2_cout, add_1bit_3_cout, xnor_1_out, xor_1_out;

  xnor xnor_1 (xnor_1_out, B[3], A[3]);
  Add_1Bit add_1bit_1 (.B(A[0]), .Cin(Cin), .Sum(Sum[0]), .A(B[0]), .Cout(add_1bit_1_cout));
  Add_1Bit add_1bit_2 (.B(A[1]), .Cin(add_1bit_1_cout), .Sum(Sum[1]), .A(B[1]), .Cout(add_1bit_2_cout));
  Add_1Bit add_1bit_3 (.B(A[2]), .Cin(add_1bit_2_cout), .Sum(Sum[2]), .A(B[2]), .Cout(add_1bit_3_cout));
  Add_1Bit add_1bit_4 (.B(A[3]), .Cin(add_1bit_3_cout), .Sum(Sum[3]), .A(B[3]));  // open: Cout
  xor xor_1 (xor_1_out, Sum[3], B[3]);
  and and_1 (Overflow, xor_1_out, xnor_1_out);
endmodule

module Half_Adder (
  input  A,
  input  B,
  output Sum,
  output Cout
);

  wire not_1_out, or_1_out;

  or or_1 (or_1_out, A, B);
  and and_1 (Cout, B, A);
  and and_2 (Sum, or_1_out, not_1_out);
  not not_1 (not_1_out, Cout);
endmodule

module TwoSComplementConvert (
  input  Flip,
  input  [3:0] Bin,
  output [3:0] Bout
);

  xor xor_1 (Bout[0], Bin[0], Flip);
  xor xor_2 (Bout[1], Bin[1], Flip);
  xor xor_3 (Bout[2], Bin[2], Flip);
  xor xor_4 (Bout[3], Bin[3], Flip);
endmodule

module IsZero (
  input  [3:0] Ain,
  output ZeroOut
);

  wire and_1_out, and_2_out, and_3_out, and_4_out, or_1_out;

  and and_1 (and_1_out, Ain[0], 1'b1);
  and and_2 (and_2_out, Ain[1], 1'b1);
  and and_3 (and_3_out, Ain[2], 1'b1);
  and and_4 (and_4_out, Ain[3], 1'b1);
  or or_1 (or_1_out, and_1_out, and_2_out, and_3_out, and_4_out);
  not not_1 (ZeroOut, or_1_out);
endmodule
